# Fritzing sketch ArduinoCourseConnectDcMotor (saved by Fritzing 0.8.0b)
breadboards: 2

parts:
  A2 = Arduino Uno (Rev3)
  M2 = DC Motor
  VCC1 = 4 x AAA Battery Mount
  M1 = DC Motor
  M3 = DC Motor
  VCC3 = 4 x AAA Battery Mount
  A3 = Arduino Uno (Rev3)  # not connected
  S1 = Pushbutton [package=THT]
  A4 = Arduino Uno (Rev3)
  VCC4 = 4 x AAA Battery Mount
  A5 = Arduino Uno (Rev3)
  Q4 = NPN-Transistor [package="TO92 [THT]"]
  M4 = DC Motor
  M5 = DC Motor
  VCC5 = 4 x AAA Battery Mount
  Q5 = NPN-Transistor [package="TO92 [THT]"]
  D1 = Rectifier Diode [part_number=1N4001 package="300 mil [THT]"]

nets:
  N1: A2.A0, M2.pin_2
  N2: A2.GND, M2.pin_1
  N3: VCC1.-, M1.pin_1
  N4: VCC1.+, M1.pin_2
  N5: M3.pin_1, VCC3.-
  N6: M3.pin_2, S1.leg0
  N7: VCC3.+, S1.leg1
  N8: A4.GND, VCC4.-, Q4.E
  N9: A4.D2, Q4.B
  N10: VCC4.+, M4.pin_1
  N11: A5.GND, VCC5.-, Q5.E
  N12: A5.D2, Q5.B
  N13: Q4.C, M4.pin_2
  N14: M5.pin_1, VCC5.+
  N15: M5.pin_2, D1.anode
  N16: Q5.C, D1.cathode

notes:
  Naief
  NIET DOEN!
  5 V
  Correct
  'Arduino drukt
  op de knop'
  Naief
  NIET DOEN
  E B C
  • C: Collector ('kollektor'): naar vermogensbron
  • B: Base ('bees'): aansturing door Arduino
  • E: Emittor ('iemittor'): naar Aarde
  Diode is een een-richtingsweg voor stroom
