# Fritzing sketch ArduinoCourseConnectLed (saved by Fritzing 0.8.0b)
breadboards: 1

parts:
  Part1 = Arduino Uno (Rev3)
  LED1 = LED - 5mm [color="Red (633nm)" package="5 mm [THT]"]
  R1 = Resistor [tolerance=±5% resistance=0 package=THT]

nets:
  N1: Part1.GND, LED1.cathode
  N2: Part1.5V, R1.Pin_0
  N3: LED1.anode, R1.Pin_1

notes:
  Weerstand
  is geheim
