# Fritzing sketch ArduinoCourseProjectColorSensor (saved by Fritzing 0.8.0b)
breadboards: 4

parts:
  Onderdeel1 = Arduino Uno (Rev3)
  R1 = Photocell (LDR) [package=THT]
  Onderdeel2 = Arduino Uno (Rev3)
  R2 = Photocell (LDR) [package=THT]
  R3 = Resistor [tolerance=±5% resistance=1k package=THT]
  LED1 = RGB LED (com. cathode, rgb) [package="5 mm [THT]"]
  Onderdeel3 = Arduino Uno (Rev3)
  LED2 = RGB LED (com. cathode, rgb) [package="5 mm [THT]"]
  Onderdeel4 = Arduino Uno (Rev3)
  R7 = Resistor [tolerance=±5% resistance=1k package=THT]
  R8 = Resistor [tolerance=±5% resistance=1k package=THT]
  R9 = Resistor [tolerance=±5% resistance=1k package=THT]

nets:
  N1: Onderdeel1.A0, R1.pin_1
  N2: Onderdeel1.5V, R1.pin_0
  N3: Onderdeel2.A0, R2.pin_1, R3.Pin_0
  N4: Onderdeel2.GND, R3.Pin_1
  N5: Onderdeel2.5V, R2.pin_0
  N6: LED1.red_anode, Onderdeel3.ICSP_MOSI, Onderdeel3.D11_PWM/MOSI
  N7: LED1.common_cathode, Onderdeel3.GND
  N8: LED1.green_anode, Onderdeel3.D10_PWM/SS
  N9: LED1.blue_anode, Onderdeel3.D9_PWM
  N10: LED2.red_anode, R7.Pin_0
  N11: LED2.common_cathode, Onderdeel4.GND
  N12: LED2.green_anode, R9.Pin_0
  N13: LED2.blue_anode, R8.Pin_0
  N14: Onderdeel4.ICSP_MOSI, Onderdeel4.D11_PWM/MOSI, R7.Pin_1
  N15: Onderdeel4.D9_PWM, R8.Pin_1
  N16: Onderdeel4.D10_PWM/SS, R9.Pin_1

notes:
  Naief: welke waarde zul je altijd meten op A0?
  De langste pin moet naar GND. De andere pinnen moeten naar een Arduino pin met een golfje
  ONJUIST!
  De langste pin moet naar GND. De andere pinnen moeten naar een Arduino pin met een golfje
