# Fritzing sketch ArduinoCourseReadInput (saved by Fritzing 0.8.0b)
breadboards: 2

parts:
  Part1 = Arduino Uno (Rev3)
  S1 = Pushbutton [package=THT]
  Part2 = Arduino Uno (Rev3)
  S2 = Pushbutton [package=THT]
  R1 = Resistor [tolerance=±5% resistance=1k package=THT]

nets:
  N1: Part1.D2, S1.leg0, R1.Pin_0
  N2: Part1.5V, S1.leg1
  N3: Part1.GND, R1.Pin_1
  N4: Part2.D2, S2.leg0
  N5: Part2.5V, S2.leg1

notes:
  Goed: pull down weerstand
  Goed bedoeld, maar onjuist!
