# Fritzing sketch ArduinoIsp (saved by Fritzing 0.8.7b)
circuit board: 8cm x 12cm

parts:
  ArduinoPassive = Arduino Uno (Rev3)
  ArduinoActive = Arduino Uno (Rev3)
  C1 = Electrolytic Capacitor [capacitance=10µF package="100 mil [THT, electrolytic]"]

nets:
  N1: ArduinoPassive.D11_PWM/MOSI, ArduinoActive.D11_PWM/MOSI
  N2: ArduinoPassive.D12/MISO, ArduinoActive.D12/MISO
  N3: ArduinoPassive.D13/SCK, ArduinoActive.D13/SCK
  N4: ArduinoPassive.RESET, ArduinoActive.D10_PWM/SS
  5V: ArduinoPassive.5V, ArduinoActive.5V
  GND: ArduinoPassive.GND, ArduinoActive.GND, C1.-
  N5: ArduinoActive.RESET, C1.+

notes:
  Passive Arduino, holding the chip to be programmed
  Active Arduino, the programmer
