# Fritzing sketch ShiftRegistersSN74HC595 (saved by Fritzing 0.8.7b)
breadboards: 4

parts:
  U1 = Mystery Part - 16 pins [chip_label=SN74HC595 package=THT]
  Part1 = Arduino Uno (Rev3)
  U2 = Mystery Part - 16 pins [chip_label=SN74HC595 package=THT]

nets:
  N1: U1.pin8, U1.pin13, Part1.GND, U2.pin8, U2.pin13
  N2: U1.pin10, U1.pin16, Part1.5V, U2.pin10, U2.pin16
  N3: U1.pin11, Part1.D4, U2.pin11
  N4: U1.pin12, Part1.D3_PWM, U2.pin12
  N5: U1.pin14, U2.pin9
  N6: Part1.D2, U2.pin14

notes:
  Hiero je andere acht verbindingen
  Arduino D2 = data pin = SER of SN74HC595
  Arduino D3 = latch pin = RCLK of SN74HC595
  Arduino D4 = clock pin = SRCLK of SN74HC595
  SN74HC595
  16 15 14 13 12 11 10 9
  | | | | | | | |
  +--+--+--+--+--+--+--+
  |> |
  +--+--+--+--+--+--+--+
  | | | | | | | |
  1 2 3 4 5 6 7 8
  Officiele pin namen:
  1: Q2
  2: Q3
  3: Q4
  3: Q5
  5: Q6
  6: Q7
  7: Q8
  8: GND
  9: QH* (voor daisy chaining)
  10: SRCLR* (naar 5V)
  11: SRCLK (naar D4): clock pin
  12: RCLK (naar D3): latch pin
  13: OE* (naar GND)
  14: SER (naar D2): data pin
  15: Q1
  16: VCC (naar 5V)
  SN74HC595
  16 15 14 13 12 11 10 9
  | | | | | | | |
  +--+--+--+--+--+--+--+
  |> |
  +--+--+--+--+--+--+--+
  | | | | | | | |
  1 2 3 4 5 6 7 8
  Verbindingen:
  1: LED 2
  2: LED 3
  3: LED 4
  3: LED 5
  5: LED 6
  6: LED 7
  7: LED 8
  8: GND
  9: daisy chaining
  10: naar 5V
  11: naar D4: clock pin
  12: naar D3: latch pin
  13: naar GND
  14: naar D2: data pin
  15: naar LED1
  16: naar 5V
  const int datapin = 2;
  const int latchpin = 3;
  const int clockpin = 4;
  void setup()
  {
  pinMode(datapin, OUTPUT);
  pinMode(latchpin, OUTPUT);
  pinMode(clockpin, OUTPUT);
  }
  void loop()
  {
  for (byte i=0; i!=256; ++i)
  {
  //Laat het getal i als binair zien
  ShowBinary(i);
  delay(100);
  }
  }
  void ShowBinary(const byte getal)
  {
  // Stuur de data naar het shift register
  shiftOut(datapin, clockpin, MSBFIRST, getal);
  // Zet de latch aan en uit, zodat de outputs aan gaan
  digitalWrite(latchpin, HIGH);
  digitalWrite(latchpin, LOW);
  }
  Hiero je acht verbindingen
  Deze orangje draad is de daisy chain!

custom parts:
  Mystery Part - 16 pins: A dummy, proxy, ersatz, stand-in part for whatever you want. With 16 pins on a 300mil inline pin header footprint.
