# Fritzing sketch 7SegmentDisplay (saved by Fritzing 0.8.7b)
breadboards: 1

parts:
  R1 = Resistor [tolerance=±5% resistance=220 package=THT]
  R2 = Resistor [tolerance=±5% resistance=220 package=THT]
  R3 = Resistor [tolerance=±5% resistance=220 package=THT]
  R4 = Resistor [tolerance=±5% resistance=220 package=THT]
  R5 = Resistor [tolerance=±5% resistance=220 package=THT]
  R6 = Resistor [tolerance=±5% resistance=220 package=THT]
  R7 = Resistor [tolerance=±5% resistance=220 package=THT]
  R8 = Resistor [tolerance=±5% resistance=220 package=THT]
  IC1 = IC, DIP package, 14 pins [chip_label=IC]
  ArduinoKid = Arduino Uno (Rev3)

nets:
  N1: R1.Pin_0, ArduinoKid.D2
  N2: R1.Pin_1, IC1.pin1
  N3: R2.Pin_0, ArduinoKid.D7
  N4: R2.Pin_1, IC1.pin2
  N5: R3.Pin_0, ArduinoKid.D6_PWM
  N6: R3.Pin_1, IC1.pin7
  N7: R4.Pin_1, IC1.pin6
  N8: R5.Pin_0, IC1.pin10
  N9: R5.Pin_1, ArduinoKid.D4
  N10: R6.Pin_0, IC1.pin8
  N11: R6.Pin_1, ArduinoKid.D5_PWM
  N12: R7.Pin_0, IC1.pin13
  N13: R7.Pin_1, ArduinoKid.D3_PWM
  N14: R8.Pin_0, IC1.pin11
  N15: R8.Pin_1, ArduinoKid.D8

notes:
  This IC is a placeholder for a 7-segment display
  +A+
  F B
  +G+
  E C
  +D+
  1: A
  2: F
  3:
  4:
  5:
  6: Option for left dot
  7: E
  8: D
  9: Right dot
  10: C
  11: G
  12:
  13: B
  14: GND
