# Fritzing sketch AnalogRead (saved by Fritzing 0.8.7b)
breadboards: 5

parts:
  R4 = Resistor [tolerance=±5% resistance=1k package=THT]
  R5 = Resistor [tolerance=±5% resistance=1k package=THT]
  R6 = Resistor [tolerance=±5% resistance=1k package=THT]
  R7 = Resistor [tolerance=±5% resistance=1k package=THT]
  R8 = Resistor [tolerance=±5% resistance=1k package=THT]
  R9 = Resistor [tolerance=±5% resistance=10k package=THT]
  R10 = Resistor [tolerance=±5% resistance=10k package=THT]
  R11 = Resistor [tolerance=±5% resistance=1k package=THT]
  R12 = Resistor [tolerance=±5% resistance=1k package=THT]
  R13 = Resistor [tolerance=±5% resistance=1k package=THT]
  part = Resistor [tolerance=±5% resistance=220 package=THT]  # not connected
  A5 = Arduino Uno (Rev3)
  A1 = Arduino Uno (Rev3)
  A2 = Arduino Uno (Rev3)
  A4 = Arduino Uno (Rev3)
  A3 = Arduino Uno (Rev3)

nets:
  N1: R4.Pin_0, R6.Pin_0
  N2: R4.Pin_1, A1.A0
  N3: R5.Pin_0, R7.Pin_0, A2.A0
  N4: R5.Pin_1, A2.GND
  N5: R6.Pin_1, A1.5V
  N6: R7.Pin_1, A2.5V
  N7: R8.Pin_0, R9.Pin_0, A3.A0
  N8: R8.Pin_1, A3.GND
  N9: R9.Pin_1, A3.5V
  N10: R10.Pin_0, R11.Pin_0, A4.A0
  N11: R10.Pin_1, A4.GND
  N12: R11.Pin_1, A4.5V
  N13: R12.Pin_0, R13.Pin_0
  N14: R12.Pin_1, A5.GND
  N15: R13.Pin_1, A5.A0

notes:
  1: Twee weerstanden van 1 kOhm achter elkaar, vanaf 5 Volt
  2: Tussen twee gelijke weerstanden van 1 kOhm in
  3: Tussen twee verschillende weerstanden in:
  10 kOhm, dan 1 kOhm
  4: Tussen twee verschillende weerstanden in:
  1 kOhm, dan 10 kOhm
  5: Twee weerstanden van 1 kOhm achter elkaar, vanaf Aarde
