# Fritzing sketch ArduinoCourseConnect7SegmentDisplay (saved by Fritzing 0.9.0b)
breadboards: 1

parts:
  R1 = Resistor [tolerance=±5% resistance=220 package=THT]
  R2 = Resistor [tolerance=±5% resistance=220 package=THT]
  R3 = Resistor [tolerance=±5% resistance=220 package=THT]
  R4 = Resistor [tolerance=±5% resistance=220 package=THT]
  R5 = Resistor [tolerance=±5% resistance=220 package=THT]
  R6 = Resistor [tolerance=±5% resistance=220 package=THT]
  R7 = Resistor [tolerance=±5% resistance=220 package=THT]
  R8 = Resistor [tolerance=±5% resistance=220 package=THT]
  IC1 = IC, DIP package, 14 pins [chip_label=IC]
  Part1 = Arduino Uno (Rev3)

nets:
  N1: R1.Pin_0, Part1.D2
  N2: R1.Pin_1, IC1.pin1
  N3: R2.Pin_0, Part1.D7
  N4: R2.Pin_1, IC1.pin2
  N5: R3.Pin_0, Part1.D6_PWM
  N6: R3.Pin_1, IC1.pin7
  N7: R4.Pin_0, Part1.D9_PWM
  N8: R4.Pin_1, IC1.pin6
  N9: R5.Pin_0, IC1.pin10
  N10: R5.Pin_1, Part1.D4
  N11: R6.Pin_0, IC1.pin8
  N12: R6.Pin_1, Part1.D5_PWM
  N13: R7.Pin_0, IC1.pin13
  N14: R7.Pin_1, Part1.D3_PWM
  N15: R8.Pin_0, IC1.pin11
  N16: R8.Pin_1, Part1.D8
  N17: IC1.pin14, Part1.5V

notes:
  This IC is a placeholder for a 7-segment display
  E
  +H+F+
  A G D
  +B+C+
  1: A
  2: F
  3: GND
  4: -
  5: -
  6: H
  7: E
  8: D
  9: -
  10: C
  11: G
  12: -
  13: B
  14: GND
