# Fritzing sketch ArduinoCourseConnectLcd (saved by Fritzing 0.8.5b)
circuit board: 31.677cm x 14.8245cm
breadboards: 3

parts:
  Part1 = Arduino Uno (Rev3)
  LCD1 = LCD screen
  Part2 = Arduino Uno (Rev3)
  LCD2 = LCD screen
  R1 = Rotary Potentiometer (Small) [maximum_resistance=100kΩ package=THT]
  Part3 = Arduino Uno (Rev3)
  LCD3 = LCD screen
  R2 = Resistor [tolerance=±5% resistance=220 package=THT]  # not connected

nets (from the schematic view):
  N1: Part1.D11_PWM/MOSI, LCD1.E
  N2: Part1.D12/MISO, LCD1.RS
  GND: Part1.GND, LCD1.VSS, LCD1.V0, LCD1.R/W
  N3: Part1.D2, LCD1.DB7
  N4: Part1.D3_PWM, LCD1.DB6
  N5: Part1.D4, LCD1.DB5
  N6: Part1.D5_PWM, LCD1.DB4
  5V: Part1.5V, LCD1.VDD
  N7: Part2.D11_PWM/MOSI, LCD2.E
  N8: Part2.D12/MISO, LCD2.RS
  N9: Part2.D2, LCD2.DB7
  N10: Part2.D3_PWM, LCD2.DB6
  N11: Part2.D4, LCD2.DB5
  N12: Part2.D5_PWM, LCD2.DB4
  N13: LCD2.V0, R1.wiper
  N14: Part3.D11_PWM/MOSI, LCD3.E
  N15: Part3.D12/MISO, LCD3.RS
  GND_2: Part3.GND, LCD3.VSS, LCD3.V0, LCD3.R/W, LCD3.LED-
  N16: Part3.D2, LCD3.DB7
  N17: Part3.D3_PWM, LCD3.DB6
  N18: Part3.D4, LCD3.DB5
  N19: Part3.D5_PWM, LCD3.DB4
  5V_2: Part3.5V, LCD3.VDD, LCD3.LED+

notes:
  Pin 3 (contrast) to GND
  No backlight
  Pin 3 (contrast) to potmeter
  No backlight
  Pin 3 (contrast) to GND
  Backlight connected
