# Fritzing sketch BlinkPwm (saved by Fritzing 0.9.0b)
circuit board: 16.9333cm x 5.64444cm
breadboards: 1

parts:
  LED1 = LED - 5mm [color="Red (633nm)" package="5 mm [THT]"]
  R1 = Resistor [tolerance=±5% resistance=1k package=THT]
  Part1 = Arduino Uno (Rev3)

nets:
  N1: LED1.cathode, R1.Pin_0
  N2: LED1.anode, Part1.D9_PWM
  N3: R1.Pin_1, Part1.GND

notes:
  1000 Ohm
