# Fritzing sketch CapacitiveSensor (saved by Fritzing 0.8.7b)
breadboards: 1

parts:
  RHelper = Resistor [tolerance=±5% resistance=1M package=THT]
  RSensor = Resistor [tolerance=±5% resistance=1k package=THT]
  RTouch = Resistor [tolerance=±5% resistance=0 package=THT]
  Part1 = Arduino Uno (Rev3)

nets:
  N1: RHelper.Pin_0, RSensor.Pin_1, RTouch.Pin_1
  N2: RHelper.Pin_1, Part1.D4
  N3: RSensor.Pin_0, Part1.D2
