# Fritzing sketch CapacitiveSensors (saved by Fritzing 0.9.0b)
breadboards: 2

parts:
  RHL = Resistor [tolerance=±5% resistance=1M package=THT]
  RSL = Resistor [tolerance=±5% resistance=1k package=THT]
  RTL = Resistor [tolerance=±5% resistance=0 package=THT]
  Part1 = Arduino Uno (Rev3)
  RHR = Resistor [tolerance=±5% resistance=1M package=THT]
  RSR = Resistor [tolerance=±5% resistance=1k package=THT]
  RTR = Resistor [tolerance=±5% resistance=0 package=THT]
  Part2 = Arduino Uno (Rev3)
  RHR1 = Resistor [tolerance=±5% resistance=1M package=THT]
  RHL1 = Resistor [tolerance=±5% resistance=1M package=THT]
  RSR1 = Resistor [tolerance=±5% resistance=1k package=THT]
  RSL1 = Resistor [tolerance=±5% resistance=1k package=THT]
  RTL1 = Resistor [tolerance=±5% resistance=0 package=THT]
  RTL2 = Resistor [tolerance=±5% resistance=0 package=THT]

nets:
  N1: RHL.Pin_0, RSL.Pin_1, RTL.Pin_1
  N2: RHL.Pin_1, Part1.D4, RHR.Pin_0
  N3: RSL.Pin_0, Part1.D2
  N4: Part1.D6_PWM, RSR.Pin_1
  N5: RHR.Pin_1, RSR.Pin_0, RTR.Pin_1
  N6: Part2.D8, RHR1.Pin_0
  N7: Part2.D2, RSL1.Pin_0
  N8: Part2.D4, RHL1.Pin_1
  N9: Part2.D6_PWM, RSR1.Pin_1
  N10: RHR1.Pin_1, RSR1.Pin_0, RTL2.Pin_1
  N11: RHL1.Pin_0, RSL1.Pin_1, RTL1.Pin_1
