# Fritzing sketch Drukknop (saved by Fritzing 0.8.7b)
breadboards: 4

parts:
  S1 = Pushbutton [package=THT]
  S3 = Pushbutton [package=THT]
  R1 = Resistor [tolerance=±5% resistance=10k package=THT]
  A1 = Arduino Uno (Rev3)
  A2 = Arduino Uno (Rev3)
  A3 = Arduino Uno (Rev3)
  A4 = Arduino Uno (Rev3)
  R2 = Resistor [tolerance=±5% resistance=10k package=THT]
  S6 = Pushbutton [package="[THT]"]
  S7 = Pushbutton [package="[THT]"]

nets:
  N1: S1.leg0, A1.A0
  N2: S1.leg1, A1.5V
  N3: S3.leg0, R1.Pin_0, A2.A0
  N4: S3.leg1, A2.5V
  N5: R1.Pin_1, A2.GND
  N6: A3.A0, S6.Pin_1, S6.Pin_2
  N7: A3.5V, S6.Pin_3, S6.Pin_4
  N8: A4.A0, R2.Pin_0, S7.Pin_1, S7.Pin_2
  N9: A4.GND, R2.Pin_1
  N10: A4.5V, S7.Pin_3, S7.Pin_4

notes:
  Goed: pull down weerstand
  Goed bedoeld, maar onjuist!
