# Fritzing sketch LES 1B. RGB - LED (saved by Fritzing 0.9.2b)
breadboards: 1

parts:
  Part2 = Arduino Uno (Rev3)
  LED1 = RGB LED (com. cathode, rgb) [package="5 mm [THT]"]
  R1 = Resistor [tolerance=±5% resistance=330 package=THT]
  R2 = Resistor [tolerance=±5% resistance=330 package=THT]
  R3 = Resistor [tolerance=±5% resistance=330 package=THT]

nets:
  N1: Part2.GND, LED1.common_cathode
  N2: LED1.red_anode, R1.Pin_0
  N3: LED1.green_anode, R2.Pin_0
  N4: LED1.blue_anode, R3.Pin_0

notes:
  Componenten:
  * Arduino UNO + breadboard
  * RGB Led
  * 3 weerstanden (220 of 330 Ohm)
  * snoeren
