# Fritzing sketch LES 1C. ROOD GROEN BLAUW (MEER KLEUR) (saved by Fritzing 0.9.2b)
breadboards: 1

parts:
  Part2 = Arduino Uno (Rev3)
  LED7 = LED - 5mm [color="Blue (430nm)" package="5 mm [THT]"]
  LED8 = LED - 5mm [color="Green (555nm)" package="5 mm [THT]"]
  LED9 = LED - 5mm [color="Red (633nm)" package="5 mm [THT]"]
  R12 = Resistor [tolerance=±5% resistance=330 package=THT]
  R13 = Resistor [tolerance=±5% resistance=330 package=THT]
  R14 = Resistor [tolerance=±5% resistance=330 package=THT]

nets:
  N1: Part2.D9_PWM, LED7.anode
  N2: Part2.D10_PWM/SS, LED8.anode
  N3: Part2.D11_PWM/MOSI, LED9.anode
  N4: LED7.cathode, R14.Pin_0
  N5: LED8.cathode, R13.Pin_0
  N6: LED9.cathode, R12.Pin_0
  N7: R12.Pin_1, R13.Pin_1, R14.Pin_1

notes:
  Componenten:
  * Arduino UNO + breadboard
  * 1 rode led, 1 groene led, 1blauwe led
  * 3 weerstanden (220 of 330 Ohm)
  * snoeren
