# Fritzing sketch LES 1D. LOOPLICHT (saved by Fritzing 0.9.2b)
breadboards: 1

parts:
  Part2 = Arduino Uno (Rev3)
  LED2 = LED - 5mm [color="Red (633nm)" package="5 mm [THT]"]
  LED3 = LED - 5mm [color="Red (633nm)" package="5 mm [THT]"]
  LED4 = LED - 5mm [color="Red (633nm)" package="5 mm [THT]"]
  LED5 = LED - 5mm [color="Red (633nm)" package="5 mm [THT]"]
  LED6 = LED - 5mm [color="Red (633nm)" package="5 mm [THT]"]
  LED7 = LED - 5mm [color="Red (633nm)" package="5 mm [THT]"]
  LED8 = LED - 5mm [color="Red (633nm)" package="5 mm [THT]"]
  LED9 = LED - 5mm [color="Red (633nm)" package="5 mm [THT]"]
  R1 = Resistor [tolerance=±5% resistance=330 package=THT]
  R2 = Resistor [tolerance=±5% resistance=330 package=THT]
  R3 = Resistor [tolerance=±5% resistance=330 package=THT]
  R4 = Resistor [tolerance=±5% resistance=330 package=THT]
  R5 = Resistor [tolerance=±5% resistance=330 package=THT]
  R6 = Resistor [tolerance=±5% resistance=330 package=THT]
  R7 = Resistor [tolerance=±5% resistance=330 package=THT]
  R8 = Resistor [tolerance=±5% resistance=330 package=THT]

nets:
  N1: Part2.D8, R2.Pin_1
  N2: Part2.D9_PWM, R7.Pin_1
  N3: Part2.D10_PWM/SS, R6.Pin_1
  N4: Part2.D11_PWM/MOSI, R5.Pin_1
  N5: Part2.GND, LED2.cathode, LED3.cathode, LED4.cathode, LED5.cathode, LED6.cathode, LED7.cathode, LED8.cathode, LED9.cathode
  N6: Part2.D4, R4.Pin_1
  N7: Part2.D5_PWM, R8.Pin_1
  N8: Part2.D6_PWM, R3.Pin_1
  N9: Part2.D7, R1.Pin_1
  N10: LED2.anode, R5.Pin_0
  N11: LED3.anode, R6.Pin_0
  N12: LED4.anode, R7.Pin_0
  N13: LED5.anode, R2.Pin_0
  N14: LED6.anode, R1.Pin_0
  N15: LED7.anode, R3.Pin_0
  N16: LED8.anode, R8.Pin_0
  N17: LED9.anode, R4.Pin_0

notes:
  Componenten:
  * Arduino UNO + breadboard
  * 8 rodeleds
  * 8 weerstanden (220 of 330 Ohm)
  4) Snoeren
