# Fritzing sketch LES 2. TWEE KNOPPEN (saved by Fritzing 0.9.2b)
breadboards: 1

parts:
  Part2 = Arduino Uno (Rev3)
  LED2 = LED - 5mm [color="Red (633nm)" package="5 mm [THT]"]
  R1 = Resistor [tolerance=±5% resistance=330 package=THT]
  S1 = Pushbutton [package="[THT]"]
  R2 = Resistor [tolerance=±5% resistance=10k package=THT]
  S2 = Pushbutton [package="[THT]"]
  R3 = Resistor [tolerance=±5% resistance=10k package=THT]

nets:
  N1: Part2.D13/SCK, LED2.anode
  N2: Part2.D2, S1.Pin_1, S1.Pin_2, R2.Pin_0
  N3: Part2.D3_PWM, S2.Pin_1, S2.Pin_2, R3.Pin_0
  N4: Part2.5V, S1.Pin_3, S1.Pin_4, S2.Pin_3, S2.Pin_4
  N5: Part2.GND, R1.Pin_0, R2.Pin_1, R3.Pin_1
  N6: LED2.cathode, R1.Pin_1

notes:
  Componenten:
  * Arduino UNO+ breadboard
  * 1 rode led
  * 1 weerstand 330 Ohm
  * 2 weerstanden 10K Ohm
  * 2 druknoppen
  * snoeren
