# Fritzing sketch LES 3. TWEE SERVO'S MET KNOPPEN (saved by Fritzing 0.9.2b)
breadboards: 1

parts:
  Part2 = Arduino Uno (Rev3)
  S1 = Pushbutton [package="[THT]"]
  S2 = Pushbutton [package="[THT]"]
  R3 = Resistor [tolerance=±5% resistance=10k package=THT]
  VCC1 = Battery
  J1 = Basic Servo
  J2 = Basic Servo
  R4 = Resistor [tolerance=±5% resistance=10k package=THT]

nets:
  N1: Part2.D9_PWM, J2.pulse
  N2: Part2.D10_PWM/SS, J1.pulse
  GND: Part2.GND, R3.Pin_1, VCC1.-, J1.gnd, J2.gnd, R4.Pin_1
  N3: S1.Pin_1, S1.Pin_2
  N4: S1.Pin_3, S1.Pin_4, R4.Pin_0
  N5: S2.Pin_1, S2.Pin_2
  N6: S2.Pin_3, S2.Pin_4, R3.Pin_0
  VCC: VCC1.+, J1.vcc, J2.vcc

notes:
  Componenten:
  * Arduino UNO + breadboard
  * 1 voeding 4,5 Volt
  * 2 servomotoren
  * 2 druknoppen
  * 2 weerstanden 10K Ohm
  * snoeren
