# Fritzing sketch LES 3. TWEE SERVO'S MET TWEE KNOPPEN (saved by Fritzing 0.9.2b)
breadboards: 1

parts:
  Part2 = Arduino Uno (Rev3)
  J1 = Basic Servo
  J2 = Basic Servo  # not connected
  J3 = Basic Servo  # not connected
  J4 = Basic Servo  # not connected
  VCC1 = Battery
  S1 = Pushbutton [package="[THT]"]
  S2 = Pushbutton [package="[THT]"]
  R2 = Resistor [tolerance=±5% resistance=10k package=THT]
  J5 = Basic Servo
  R3 = Resistor [tolerance=±5% resistance=10k package=THT]

nets:
  N1: Part2.D8, S1.Pin_3, S1.Pin_4, R3.Pin_0
  N2: Part2.D9_PWM, J5.pulse
  N3: Part2.D10_PWM/SS, J1.pulse
  N4: Part2.D7, S2.Pin_3, S2.Pin_4, R2.Pin_0
  N5: Part2.5V, S1.Pin_1, S1.Pin_2, S2.Pin_1, S2.Pin_2
  N6: Part2.GND, R2.Pin_1, R3.Pin_1
  GND: J1.gnd, VCC1.-, J5.gnd
  VCC: J1.vcc, VCC1.+, J5.vcc

notes:
  Componenten:
  1. Arduino UNO+Breadboard
  2) 2 Servomotoren
  3) 2 Knoppen
  4) 2 Weerstanden 10K
  5) 1 Voeding 4.5 Volt
  4) Snoeren
