# Fritzing sketch LES 4. FSR MET SERVO (saved by Fritzing 0.9.2b)
breadboards: 1

parts:
  Part2 = Arduino Uno (Rev3)
  J1 = Basic Force Sensing Resistor (FSR) [package=THT]
  R2 = Resistor [tolerance=±5% resistance=10k package=THT]
  J2 = Basic Servo

nets:
  N1: Part2.A0, J1.pin_0, R2.Pin_0
  N2: Part2.D9_PWM, J2.pulse
  5V: Part2.5V, J1.pin_1, J2.vcc
  GND: Part2.GND, R2.Pin_1, J2.gnd

notes:
  Componenten:
  * Arduino UNO + breadboard
  * 1 servomotor
  * 1 FSR
  * 1 weerstand 10K Ohm
  * snoeren
