# Fritzing sketch LES 6. MUZIEKTONE (saved by Fritzing 0.9.2b)
breadboards: 1

parts:
  Part2 = Arduino Uno (Rev3)
  R1 = Resistor [tolerance=±5% resistance=100 package=THT]
  SPKR1 = Loudspeaker

nets:
  N1: Part2.D11_PWM/MOSI, SPKR1.pin2
  N2: Part2.GND, R1.Pin_0
  N3: R1.Pin_1, SPKR1.pin1

notes:
  Componenten:
  1) Arduino UNO+Breadboard
  2) sPEAKER 8 oHM
  3) 1 Weerstand
  (100 Ohm)
  4) Snoeren
