# Fritzing sketch LES 6. TONE SIMPEL (saved by Fritzing 0.9.2b)
breadboards: 1

parts:
  Part2 = Arduino Uno (Rev3)
  R1 = Resistor [tolerance=±5% resistance=100 package=THT]
  SPKR1 = Loudspeaker

nets:
  N1: Part2.D8, SPKR1.pin2
  N2: Part2.GND, R1.Pin_1
  N3: R1.Pin_0, SPKR1.pin1

notes:
  Componenten:
  * Arduino UNO + breadboard
  * 1 speaker 8 Ohm
  * 1 weerstand 100 Ohm
  * snoeren
