# Fritzing sketch LES 7. RELAIS MET 2 LEDS (saved by Fritzing 0.9.2b)
breadboards: 1

parts:
  Part2 = Arduino Uno (Rev3)
  Q1 = NPN-Transistor [package="TO92 [THT]"]  # not connected
  R2 = Resistor [tolerance=±5% resistance=1k package=THT]  # not connected
  D1 = Rectifier Diode [part_number=1N4001 package="300 mil [THT]"]
  DIP-Relay1 = DIP-Relay-D31A [part_number=D31A*]
  LED1 = LED - 5mm [color="Red (633nm)" package="5 mm [THT]"]
  LED2 = LED - 5mm [color="Green (555nm)" package="5 mm [THT]"]
  R4 = Resistor [tolerance=±5% resistance=330 package=THT]
  R5 = Resistor [tolerance=±5% resistance=330 package=THT]

nets:
  N1: Part2.5V, D1.cathode, DIP-Relay1.A2_Switch_Terminal_A, R4.Pin_1, R5.Pin_1
  N2: D1.anode, DIP-Relay1.A1_Switch_Terminal_A
  N3: DIP-Relay1.B1_Switch_Terminal_B, LED2.anode
  N4: LED1.cathode, R5.Pin_0
  N5: LED2.cathode, R4.Pin_0

notes:
  Componenten:
  * Arduino UNO + breadboard
  * 1 rode led, 1 groene led
  * 2 weerstanden 330 Ohm, 1 weerstand 1K Ohm
  * 1 relais
  * 1 diode 1N4001
  * 1 Transistor 547
  (cbe: collector, basis, emitter)
  * 1 weerstand 1K Ohm
  * snoeren
