# Fritzing sketch LES 7. RELAIS (saved by Fritzing 0.9.2b)
breadboards: 1

parts:
  Part2 = Arduino Uno (Rev3)
  Q1 = NPN-Transistor [package="TO92 [THT]"]  # not connected
  R2 = Resistor [tolerance=±5% resistance=1k package=THT]  # not connected
  D1 = Rectifier Diode [part_number=1N4001 package="300 mil [THT]"]
  DIP-Relay1 = DIP-Relay-D31A [part_number=D31A*]

nets:
  N1: Part2.5V, D1.cathode, DIP-Relay1.A2_Switch_Terminal_A
  N2: D1.anode, DIP-Relay1.A1_Switch_Terminal_A

notes:
  Componenten:
  * Arduino UNO + breadboard
  * 1 weerstand 1K Ohm
  * 1 relais
  * 1 diode 1N4001
  * 1 Transistor 547
  (cbe: collector, basis, emitter)
  * 1 weerstand 1K Ohm
  * snoeren
