# Fritzing sketch LES 8. SHARP IR UITLEZEN (saved by Fritzing 0.9.2b)
breadboards: 1

parts:
  Part2 = Arduino Uno (Rev3)
  R1 = Resistor [tolerance=±5% resistance=100 package=THT]
  SPKR1 = Loudspeaker
  J2 = Infrared Proximity Sensor

nets:
  N1: Part2.A0, J2.Vout
  N2: Part2.D9_PWM, R1.Pin_1
  5V: Part2.5V, J2.Vcc
  GND: Part2.GND, SPKR1.pin1, J2.GND
  N3: R1.Pin_0, SPKR1.pin2

notes:
  Componenten:
  * Arduino UNO + breadboard
  * 1 speaker 8 Watt
  * IR-sensor Sharp 2YOa21
  * 1 weerstand (100 Ohm)
  * snoeren
