# Fritzing sketch LES 9. LDR MET THRESHOLD (saved by Fritzing 0.9.2b)
breadboards: 1

parts:
  Part2 = Arduino Uno (Rev3)
  LED2 = LED - 5mm [color="Red (633nm)" package="5 mm [THT]"]
  R1 = Resistor [tolerance=±5% resistance=330 package=THT]
  R2 = Photocell (LDR) [package=THT]
  R3 = Resistor [tolerance=±5% resistance=10k package=THT]

nets:
  N1: Part2.A0, R2.pin_0, R3.Pin_0
  N2: Part2.D11_PWM/MOSI, LED2.anode
  N3: Part2.GND, R1.Pin_0, R3.Pin_1
  N4: LED2.cathode, R1.Pin_1

notes:
  Componenten:
  * Arduino UNO + breadboard
  * 1 rode led
  * 1 LDR
  * 1 weerstand 330 Ohm, 1 weerstand 10K Ohm
  * snoeren
