# Fritzing sketch LES 9. LDR TROMMEL SERVO (saved by Fritzing 0.9.2b)
breadboards: 1

parts:
  Part2 = Arduino Uno (Rev3)
  R2 = Photocell (LDR) [package=THT]
  R3 = Resistor [tolerance=±5% resistance=10k package=THT]
  J1 = Basic Servo

nets:
  N1: Part2.A0, R2.pin_0, R3.Pin_0
  N2: Part2.D6_PWM, J1.pulse
  GND: Part2.GND, R3.Pin_1, J1.gnd
  N3: R2.pin_1, J1.vcc

notes:
  Componenten:
  * Arduino UNO + breadboard
  * 1 LDR
  * 1 servomotor
  * 1 weerstand 10K Ohm
  * snoeren
