# Fritzing sketch Lcd (saved by Fritzing 0.9.2b)
circuit board: 31.677cm x 14.8245cm
breadboards: 4

parts:
  Part1 = Arduino Uno (Rev3)
  LCD1 = LCD screen
  Part2 = Arduino Uno (Rev3)
  LCD2 = LCD screen
  R1 = Rotary Potentiometer (Small) [maximum_resistance=100kΩ package=THT]
  Part3 = Arduino Uno (Rev3)
  LCD3 = LCD screen
  part = Resistor [tolerance=±5% resistance=220 package=THT]  # not connected
  Part4 = Arduino Uno (Rev3)
  LCD4 = LCD screen
  R3 = Rotary Potentiometer (Small) [maximum_resistance=100kΩ package=THT]
  R4 = Resistor [tolerance=±5% resistance=220 package=THT]  # not connected
  R5 = Resistor [tolerance=±5% resistance=220 package=THT]
  R6 = Resistor [tolerance=±5% resistance=220 package=THT]

nets (from the breadboard view):
  N1: Part1.D11_PWM/MOSI, LCD1.E
  N2: Part1.D12/MISO, LCD1.RS
  GND: Part1.GND, LCD1.VSS, LCD1.V0, LCD1.R/W
  N3: Part1.D2, LCD1.DB7
  N4: Part1.D3_PWM, LCD1.DB6
  N5: Part1.D4, LCD1.DB5
  N6: Part1.D5_PWM, LCD1.DB4
  5V: Part1.5V, LCD1.VDD
  N7: Part2.D11_PWM/MOSI, LCD2.E
  N8: Part2.D12/MISO, LCD2.RS
  GND_2: Part2.GND, LCD2.VSS, LCD2.R/W, R1.leg1
  N9: Part2.D2, LCD2.DB7
  N10: Part2.D3_PWM, LCD2.DB6
  N11: Part2.D4, LCD2.DB5
  N12: Part2.D5_PWM, LCD2.DB4
  5V_2: Part2.5V, LCD2.VDD, R1.leg2
  N13: LCD2.V0, R1.wiper
  N14: Part3.D11_PWM/MOSI, LCD3.E
  N15: Part3.D12/MISO, LCD3.RS
  GND_3: Part3.GND, LCD3.VSS, LCD3.V0, LCD3.R/W, LCD3.LED-
  N16: Part3.D2, LCD3.DB7
  N17: Part3.D3_PWM, LCD3.DB6
  N18: Part3.D4, LCD3.DB5
  N19: Part3.D5_PWM, LCD3.DB4
  5V_3: Part3.5V, LCD3.VDD, R5.Pin_1
  N20: LCD3.LED+, R5.Pin_0
  N21: Part4.D11_PWM/MOSI, LCD4.E
  N22: Part4.D12/MISO, LCD4.RS
  GND_4: Part4.GND, LCD4.VSS, LCD4.R/W, LCD4.LED-, R3.leg1
  N23: Part4.D2, LCD4.DB7
  N24: Part4.D3_PWM, LCD4.DB6
  N25: Part4.D4, LCD4.DB5
  N26: Part4.D5_PWM, LCD4.DB4
  5V_4: Part4.5V, LCD4.VDD, R3.leg2, R6.Pin_1
  N27: LCD4.V0, R3.wiper
  N28: LCD4.LED+, R6.Pin_0

notes:
  Pin 3 (contrast) to GND
  No backlight
  Pin 3 (contrast) to potmeter
  No backlight
  Pin 3 (contrast) to GND
  Backlight connected
  Pin 3 (contrast) to potmeter
  With backlight
