# Fritzing sketch Ldr (saved by Fritzing 0.9.0b)
breadboards: 2

parts:
  R4 = Resistor [tolerance=±5% resistance=1k package=THT]
  S3 = Photocell (LDR) [package=THT]
  R5 = Resistor [tolerance=±5% resistance=1k package=THT]
  Part1 = Arduino Uno (Rev3)
  Part2 = Arduino Uno (Rev3)
  S4 = Photocell (LDR) [package=THT]

nets:
  N1: R4.Pin_0, S4.pin_1
  N2: R4.Pin_1, Part1.A0
  N3: S3.pin_0, Part2.5V
  N4: S3.pin_1, R5.Pin_1, Part2.A0
  N5: R5.Pin_0, Part2.GND
  N6: Part1.5V, S4.pin_0

notes:
  Goed bedoeld,
  maar naief
  Juist
