# Fritzing sketch LedOefening (saved by Fritzing 0.8.7b)
circuit board: 8cm x 8cm
circuit board: 8cm x 8cm
circuit board: 8cm x 8cm
circuit board: 8cm x 8cm
circuit board: 8cm x 8cm
circuit board: 8cm x 8cm
circuit board: 8cm x 8cm
circuit board: 8cm x 8cm
breadboards: 8

parts:
  LED1 = LED - 5mm [color="Red (633nm)" package="5 mm [THT]"]
  R1 = Resistor [tolerance=±5% resistance=1k package=THT]
  Part1 = Arduino Uno (Rev3)
  Part2 = Arduino Uno (Rev3)
  LED2 = LED - 5mm [color="Red (633nm)" package="5 mm [THT]"]
  R2 = Resistor [tolerance=±5% resistance=1k package=THT]
  Part3 = Arduino Uno (Rev3)
  Part4 = Arduino Uno (Rev3)
  LED3 = LED - 5mm [color="Red (633nm)" package="5 mm [THT]"]
  LED4 = LED - 5mm [color="Red (633nm)" package="5 mm [THT]"]
  R3 = Resistor [tolerance=±5% resistance=1k package=THT]
  R4 = Resistor [tolerance=±5% resistance=1k package=THT]
  Part5 = Arduino Uno (Rev3)
  LED5 = LED - 5mm [color="Red (633nm)" package="5 mm [THT]"]
  R5 = Resistor [tolerance=±5% resistance=1k package=THT]
  Part6 = Arduino Uno (Rev3)
  LED6 = LED - 5mm [color="Red (633nm)" package="5 mm [THT]"]
  R6 = Resistor [tolerance=±5% resistance=1k package=THT]
  Part7 = Arduino Uno (Rev3)
  Part8 = Arduino Uno (Rev3)
  LED7 = LED - 5mm [color="Red (633nm)" package="5 mm [THT]"]
  LED8 = LED - 5mm [color="Red (633nm)" package="5 mm [THT]"]
  R7 = Resistor [tolerance=±5% resistance=1k package=THT]
  R8 = Resistor [tolerance=±5% resistance=1k package=THT]
  part = Resistor [tolerance=±5% resistance=220 package=THT]  # not connected

nets:
  N1: LED1.cathode, R1.Pin_1
  N2: LED1.anode, Part1.GND
  N3: R1.Pin_0, Part1.5V
  N4: Part2.5V, R2.Pin_1
  N5: Part2.GND, LED2.anode
  N6: LED2.cathode, R2.Pin_0
  N7: Part3.5V, R3.Pin_0
  N8: Part3.GND, LED3.cathode
  N9: Part4.5V, R4.Pin_1
  N10: Part4.GND, LED4.cathode
  N11: LED3.anode, R3.Pin_1
  N12: LED4.anode, R4.Pin_0
  N13: Part5.5V, LED5.cathode
  N14: Part5.GND, R5.Pin_1
  N15: LED5.anode, R5.Pin_0
  N16: Part6.5V, LED6.cathode
  N17: Part6.GND, R6.Pin_0
  N18: LED6.anode, R6.Pin_1
  N19: Part7.5V, LED7.anode
  N20: Part7.GND, R7.Pin_1
  N21: Part8.5V, LED8.anode
  N22: Part8.GND, R8.Pin_0
  N23: LED7.cathode, R7.Pin_0
  N24: LED8.cathode, R8.Pin_1

notes:
  Weerstand manier 1 - LED manier 1
  Weerstand manier 2 - LED manier 1
  Weerstand manier 1 - LED manier 2
  Weerstand manier 2 - LED manier 2
  LED manier 1 - Weerstand manier 1
  LED manier 1 - Weerstand manier 2
  LED manier 2 - Weerstand manier 2
  LED manier 2 - Weerstand manier 1
