# Fritzing sketch Les0 (saved by Fritzing 0.8.5b)
breadboards: 2

parts:
  Part2 = Arduino Uno (Rev3)
  LED2 = LED - 5mm [color="Red (633nm)" package="5 mm [THT]"]
  Part4 = Arduino Uno (Rev3)
  R3 = Resistor [tolerance=±5% resistance=1k package=THT]
  LED4 = LED - 5mm [color="Red (633nm)" package="5 mm [THT]"]
  R2 = Resistor [tolerance=±5% resistance=1k package=THT]

nets:
  N1: Part2.GND, LED2.cathode
  N2: LED2.anode, R2.Pin_0
  N3: Part4.GND, R3.Pin_0
  N4: Part4.5V, LED4.anode
  N5: R3.Pin_1, LED4.cathode
