# Fritzing sketch Piezo (saved by Fritzing 0.8.7b)
breadboards: 1

parts:
  J1 = Piezo Speaker
  Part1 = Arduino Uno (Rev3)  # not connected
  R1 = Resistor [tolerance=±5% resistance=1k package=THT]

nets:
  N1: J1.pin2, R1.Pin_0, R1.Pin_1
