# Fritzing sketch ReadInput (saved by Fritzing 0.8.7b)
breadboards: 2

parts:
  S1 = Pushbutton [package=THT]
  S3 = Pushbutton [package=THT]
  R1 = Resistor [tolerance=±5% resistance=1k package=THT]
  part = Resistor [tolerance=±5% resistance=220 package=THT]  # not connected
  A1 = Arduino Uno (Rev3)
  A2 = Arduino Uno (Rev3)

nets:
  N1: S1.leg0, A1.A0
  N2: S1.leg1, A1.5V
  N3: S3.leg0, R1.Pin_0, A2.A0
  N4: S3.leg1, A2.5V
  N5: R1.Pin_1, A2.GND

notes:
  Goed: pull down weerstand
  Goed bedoeld, maar onjuist!
