# Fritzing sketch LES 1C. FADE MET 1 LED (saved by Fritzing 0.9.2b)
breadboards: 1

parts:
  Part2 = Arduino Uno (Rev3)
  LED2 = LED - 5mm [color="Red (633nm)" package="5 mm [THT]"]
  R2 = Resistor [tolerance=±5% resistance=330 package=THT]

nets:
  N1: Part2.D9_PWM, LED2.anode
  N2: Part2.GND, R2.Pin_1
  N3: LED2.cathode, R2.Pin_0

notes:
  Componenten:
  * Arduino UNO + breadboard
  * 1 rode led
  * 1 weerstand (220 of 330 Ohm)
  * snoeren
