# Fritzing sketch LES 2. KNOP (saved by Fritzing 0.9.2b)
breadboards: 1

parts:
  Part2 = Arduino Uno (Rev3)
  LED2 = LED - 5mm [color="Red (633nm)" package="5 mm [THT]"]
  R1 = Resistor [tolerance=±5% resistance=330 package=THT]
  S1 = Pushbutton [package="[THT]"]
  R2 = Resistor [tolerance=±5% resistance=10k package=THT]

nets:
  N1: Part2.D13/SCK, LED2.anode
  N2: Part2.D2, S1.Pin_1, S1.Pin_2, R2.Pin_0
  N3: Part2.5V, S1.Pin_3, S1.Pin_4
  N4: Part2.GND, R1.Pin_0, R2.Pin_1
  N5: LED2.cathode, R1.Pin_1

notes:
  Componenten:
  * Arduino UNO + breadboard
  * 1rode led
  * 1 weerstanden 330 Ohm
  * 1 weerstand 10K Ohm
  * 1 drukknop
  * snoeren
