# Fritzing sketch LES 3. SERVO MET POTMETER (saved by Fritzing 0.9.2b)
breadboards: 1

parts:
  Part2 = Arduino Uno (Rev3)
  R1 = Rotary Potentiometer (Small) [maximum_resistance=100kΩ package=THT]
  J1 = Basic Servo

nets:
  N1: Part2.A0, R1.wiper
  N2: Part2.D9_PWM, J1.pulse
  5V: Part2.5V, R1.leg1, J1.vcc
  GND: Part2.GND, R1.leg2, J1.gnd

notes:
  Componenten:
  * Arduino UNO+ breadboard
  * 1 servomotor
  * 1 potentiometer
  * snoeren
