# Fritzing sketch LES 4. SIMPELE DRUKMETING (saved by Fritzing 0.9.2b)
breadboards: 1

parts:
  Part2 = Arduino Uno (Rev3)
  LED2 = LED - 5mm [color="Red (633nm)" package="5 mm [THT]"]
  R1 = Resistor [tolerance=±5% resistance=330 package=THT]
  J1 = Basic Force Sensing Resistor (FSR) [package=THT]
  R2 = Resistor [tolerance=±5% resistance=10k package=THT]

nets:
  N1: Part2.A0, J1.pin_0, R2.Pin_0
  N2: Part2.D11_PWM/MOSI, LED2.anode
  N3: Part2.5V, J1.pin_1
  N4: Part2.GND, R1.Pin_1, R2.Pin_1
  N5: LED2.cathode, R1.Pin_0

notes:
  Componenten:
  * Arduino UNO + breadboard
  * 1 rode led
  * 1 weerstand: 330 Ohm
  * 1 weerstand 10K Ohm
  * 1 FSR
  * Snoeren
