# Fritzing sketch LES 5. MOTOR PWM (saved by Fritzing 0.9.2b)
breadboards: 1

parts:
  Part2 = Arduino Uno (Rev3)
  Q1 = NPN-Transistor [package="TO92 [THT]"]
  R2 = Resistor [tolerance=±5% resistance=1k package=THT]
  M1 = DC Motor
  C1 = Electrolytic Capacitor [capacitance=1µF package="100 mil [THT, electrolytic]"]
  D1 = Rectifier Diode [part_number=1N4001 package="300 mil [THT]"]
  VCC1 = Battery

nets:
  N1: Part2.D3_PWM, R2.Pin_1
  N2: Q1.E, M1.pin_1, D1.anode
  N3: Q1.B, R2.Pin_0
  N4: Q1.C, C1.+, VCC1.-
  N5: M1.pin_2, C1.-, D1.cathode, VCC1.+

notes:
  Componenten:
  * Arduino UNO + breadboard
  * 1 batterijpack 4,5 Volt
  * 1 weerstand 1K Ohm
  * 1 Transistor 547
  (cbe: collector(+), basis, emitter)
  * 1 diode 1N4001
  * 1 condensator 100uF
  * snoeren
