# Fritzing sketch LES 5. TRANSISTOR (saved by Fritzing 0.9.2b)
breadboards: 1

parts:
  Part2 = Arduino Uno (Rev3)
  Q1 = NPN-Transistor [package="TO92 [THT]"]
  LED1 = LED - 5mm [color="Red (633nm)" package="5 mm [THT]"]
  R1 = Resistor [tolerance=±5% resistance=220 package=THT]
  R2 = Resistor [tolerance=±5% resistance=220 package=THT]

nets:
  N1: Part2.D3_PWM, R2.Pin_1
  N2: Part2.5V, Q1.E
  N3: Part2.GND, R1.Pin_1
  N4: Q1.B, R2.Pin_0
  N5: Q1.C, LED1.anode
  N6: LED1.cathode, R1.Pin_0

notes:
  Componenten:
  * Arduino UNO + breadboard
  * 1 rode led
  * 1 weerstand: 330 Ohm
  * 1 weerstand 1K Ohm
  * 1 Transistor 547
  (cbe: collector, basis, emitter)
  * snoeren
