# Fritzing sketch LES 7. RELAIS MET DC-MOTOR (saved by Fritzing 0.9.2b)
breadboards: 1

parts:
  Part2 = Arduino Uno (Rev3)
  Q1 = NPN-Transistor [package="TO92 [THT]"]
  R2 = Resistor [tolerance=±5% resistance=1k package=THT]
  D1 = Rectifier Diode [part_number=1N4001 package="300 mil [THT]"]
  DIP-Relay1 = DIP-Relay-D31A [part_number=D31A*]
  VCC1 = Battery
  M1 = DC Motor  # not connected

nets:
  N1: Part2.D8, R2.Pin_1
  N2: Part2.5V, D1.cathode, DIP-Relay1.A2_Switch_Terminal_A
  N3: Part2.GND, Q1.C, VCC1.-
  N4: Q1.E, D1.anode, DIP-Relay1.A1_Switch_Terminal_A
  N5: Q1.B, R2.Pin_0
  N6: DIP-Relay1.B1_Switch_Terminal_B, VCC1.+

notes:
  Componenten:
  * Arduino UNO + breadboard
  * Batterijpack 4,5 Volt
  * 1 DC motor
  * 1 relais
  * 1 diode 1N4001
  * 1 Transistor 547
  (cbe: collector, basis, emitter)
  * 1 weerstand 1K Ohm
  * snoeren
