# Fritzing sketch LES 8. OBSTAKEL ONTWIJKEND OBJECT (saved by Fritzing 0.9.2b)
breadboards: 1

parts:
  Part2 = Arduino Uno (Rev3)
  Q1 = NPN-Transistor [package="TO92 [THT]"]
  R2 = Resistor [tolerance=±5% resistance=1k package=THT]
  D1 = Rectifier Diode [part_number=1N4001 package="300 mil [THT]"]
  DIP-Relay1 = DIP-Relay-D31A [part_number=D31A*]
  VCC1 = Battery
  M1 = DC Motor  # not connected
  M2 = DC Motor
  J1 = Infrared Proximity Sensor
  S2 = Pushbutton [package=THT]

nets:
  N1: Part2.A0, J1.Vout
  N2: Part2.D13/SCK, R2.Pin_0
  5V: Part2.5V, D1.cathode, DIP-Relay1.A2_Switch_Terminal_A, J1.Vcc
  GND: Part2.GND, Q1.C, M2.pin_2, J1.GND, S2.leg0
  N3: Q1.B, R2.Pin_1
  N4: D1.anode, DIP-Relay1.A1_Switch_Terminal_A
  N5: DIP-Relay1.B1_Switch_Terminal_B, VCC1.+, M2.pin_1
  N6: VCC1.-, S2.leg1

notes:
  Componenten:
  * Arduino UNO + breadboard
  * IR-sensor Sharp 2YOa21
  * 2 DC Motoren
  * relais
  * transistor 547
  * diode 1N4001
  * drukknop
  * 1 weerstand 1K Ohm
  * snoeren
