# Fritzing sketch LES 9. LDR BLUES (saved by Fritzing 0.9.2b)
breadboards: 1

parts:
  Part2 = Arduino Uno (Rev3)
  R2 = Photocell (LDR) [package=THT]
  R4 = Photocell (LDR) [package=THT]
  R5 = Photocell (LDR) [package=THT]
  R6 = Photocell (LDR) [package=THT]
  R7 = Photocell (LDR) [package=THT]
  R17 = Resistor [tolerance=±5% resistance=100 package=THT]
  R18 = Resistor [tolerance=±5% resistance=10k package=THT]
  R19 = Resistor [tolerance=±5% resistance=10k package=THT]
  R20 = Resistor [tolerance=±5% resistance=10k package=THT]
  R21 = Resistor [tolerance=±5% resistance=10k package=THT]
  SPKR1 = Loudspeaker
  R23 = Resistor [tolerance=±5% resistance=10k package=THT]

nets:
  N1: Part2.A0, R7.pin_1, R18.Pin_0
  N2: Part2.A1, R5.pin_1, R19.Pin_0
  N3: Part2.A2, R6.pin_1, R20.Pin_0
  N4: Part2.A3, R4.pin_1, R21.Pin_0
  N5: Part2.A4/SDA, R2.pin_1, R23.Pin_0
  N6: Part2.D8, R17.Pin_1
  N7: Part2.5V, R2.pin_0, R4.pin_0, R5.pin_0, R6.pin_0, R7.pin_0
  N8: Part2.GND, R18.Pin_1, R19.Pin_1, R20.Pin_1, R21.Pin_1, SPKR1.pin1, R23.Pin_1
  N9: R17.Pin_0, SPKR1.pin2

notes:
  Componenten:
  * Arduino UNO + breadboard
  * 5 x LDR 300 KOhm
  * 1 speaker 8 Ohm
  * 5 x weerstand 10 KOhm, 1 weerstand 100 ohm
  * snoeren
