# Fritzing sketch LES 9. LDR TROMMEL SOLENOID (saved by Fritzing 0.9.2b)
breadboards: 1

parts:
  Part2 = Arduino Uno (Rev3)
  R2 = Photocell (LDR) [package=THT]
  R3 = Resistor [tolerance=±5% resistance=10k package=THT]
  L1 = Solenoid

nets:
  N1: Part2.A0, R2.pin_0, R3.Pin_0
  N2: Part2.GND, R3.Pin_1, L1.pin1
  N3: R2.pin_1, L1.pin2

notes:
  Componenten:
  * Arduino UNO + breadboard
  * 1 LDR
  * 1 Solenoid
  * 1 weerstand.........Ohm, 1 weerstand 10K Ohm
  * snoeren
