# Fritzing sketch LES 9. LDR TROMMEL (saved by Fritzing 0.9.2b)
breadboards: 1

parts:
  Part2 = Arduino Uno (Rev3)
  LED2 = LED - 5mm [color="Red (633nm)" package="5 mm [THT]"]  # not connected
  R1 = Resistor [tolerance=±5% resistance=330 package=THT]  # not connected
  R2 = Photocell (LDR) [package=THT]
  R3 = Resistor [tolerance=±5% resistance=10k package=THT]
  J1 = Basic Servo
  L1 = Solenoid  # not connected

nets:
  N1: Part2.A0, R2.pin_0, R3.Pin_0
  N2: Part2.D6_PWM, J1.pulse
  GND: Part2.GND, R3.Pin_1, J1.gnd
  N3: R2.pin_1, J1.vcc

notes:
  Componenten:
  * Arduino UNO + breadboard
  * 1 rode led
  * 1 LDR
  * 1 weerstand 330 Ohm, 1 weerstand 10K Ohm
  * snoeren
