# Fritzing sketch Sensor (saved by Fritzing 0.8.7b)
breadboards: 2

parts:
  S2 = Photocell (LDR) [package=THT]
  R4 = Resistor [tolerance=±5% resistance=1k package=THT]
  S3 = Photocell (LDR) [package=THT]
  R5 = Resistor [tolerance=±5% resistance=1k package=THT]
  Part1 = Arduino Uno (Rev3)
  Part2 = Arduino Uno (Rev3)

nets:
  N1: S2.pin_0, Part1.5V
  N2: S2.pin_1, R4.Pin_0
  N3: R4.Pin_1, Part1.A0
  N4: S3.pin_0, Part2.5V
  N5: S3.pin_1, R5.Pin_1, Part2.A0
  N6: R5.Pin_0, Part2.GND

notes:
  1: Direct op input
