# Fritzing sketch ServoMotor (saved by Fritzing 0.8.0b)
breadboards: 1

parts:
  J1 = Basic Servo
  Onderdeel1 = Arduino Uno (Rev3)

nets:
  GND: J1.gnd, Onderdeel1.GND
  VCC: J1.vcc, Onderdeel1.5V
  N1: J1.pulse, Onderdeel1.D9_PWM
