# Fritzing sketch 10_LDR (saved by Fritzing 0.9.2b)
breadboards: 2

parts:
  LED1 = LED - 5mm [color="Red (633nm)" package="5 mm [THT]"]
  Part1 = Arduino Uno (Rev3)
  R1 = Resistor [tolerance=±5% resistance=1k package=THT]  # not connected
  R2 = Resistor [tolerance=±5% resistance=10k package=THT]
  Part2 = Arduino Uno (Rev3)
  R3 = Resistor [tolerance=±5% resistance=10k package=THT]
  Part3 = Arduino Uno (Rev3)  # not connected
  R4 = Photocell (LDR) [package=THT]  # not connected
  R5 = Photocell (LDR) [package=THT]

nets:
  N1: LED1.anode, Part1.D13/SCK
  N2: Part1.A0, R2.Pin_1, R5.pin_1
  N3: Part1.GND, R2.Pin_0
  N4: Part1.5V, R5.pin_0
  N5: Part2.A0, R3.Pin_1
  N6: Part2.GND, R3.Pin_0
