# Fritzing sketch 18_7_pin_piano (saved by Fritzing 0.9.2b)
breadboards: 3

parts:
  Part3 = Arduino Uno (Rev3)
  S7 = Pushbutton [package="[THT]"]
  S8 = Pushbutton [package="[THT]"]
  S9 = Pushbutton [package="[THT]"]
  R7 = Resistor [tolerance=±5% resistance=10k package=THT]
  R8 = Resistor [tolerance=±5% resistance=10k package=THT]
  R9 = Resistor [tolerance=±5% resistance=10k package=THT]
  R10 = Resistor [tolerance=±5% resistance=10k package=THT]
  J1 = Piezo Speaker
  Part4 = Arduino Uno (Rev3)
  S10 = Pushbutton [package="[THT]"]
  S11 = Pushbutton [package="[THT]"]
  R11 = Resistor [tolerance=±5% resistance=10k package=THT]
  R12 = Resistor [tolerance=±5% resistance=10k package=THT]
  R14 = Resistor [tolerance=±5% resistance=10k package=THT]
  J2 = Piezo Speaker
  Part5 = Arduino Uno (Rev3)
  S13 = Pushbutton [package="[THT]"]
  R16 = Resistor [tolerance=±5% resistance=10k package=THT]
  R18 = Resistor [tolerance=±5% resistance=10k package=THT]
  J3 = Piezo Speaker

nets:
  N1: Part3.D8, J1.pin2
  N2: Part3.GND, R7.Pin_1, R8.Pin_1, R9.Pin_1, R10.Pin_1
  N3: Part3.D2, S9.Pin_1, S9.Pin_2, R7.Pin_0
  N4: Part3.D3_PWM, S8.Pin_1, S8.Pin_2, R9.Pin_0
  N5: Part3.D4, S7.Pin_1, S7.Pin_2, R10.Pin_0
  N6: Part3.5V, S7.Pin_3, S7.Pin_4, S8.Pin_3, S8.Pin_4, S9.Pin_3, S9.Pin_4
  N7: R8.Pin_0, J1.pin1
  N8: Part4.D8, J2.pin2
  N9: Part4.GND, R11.Pin_1, R12.Pin_1, R14.Pin_1
  N10: Part4.D2, S10.Pin_1, S10.Pin_2, R14.Pin_0
  N11: Part4.D3_PWM, S11.Pin_1, S11.Pin_2, R11.Pin_0
  N12: Part4.5V, S10.Pin_3, S10.Pin_4, S11.Pin_3, S11.Pin_4
  N13: R12.Pin_0, J2.pin1
  N14: Part5.D8, J3.pin2
  N15: Part5.GND, R16.Pin_1, R18.Pin_1
  N16: Part5.D2, S13.Pin_1, S13.Pin_2, R18.Pin_0
  N17: Part5.5V, S13.Pin_3, S13.Pin_4
  N18: R16.Pin_0, J3.pin1

notes:
  Alle weerstanden: 10 kOhm
  Bruin-Zwart-Oranje-Goud
