# Fritzing sketch 19_fig_1 (saved by Fritzing 0.9.3b)
circuit board: 8.46667cm x 5.64444cm
breadboards: 1

parts:
  J1 = Piezo Speaker
  A = Arduino Uno (Rev3)
  toets1 = Pushbutton [package="[THT]"]
  R1 = Resistor [tolerance=±5% resistance=10k package=THT]
  Rs = Resistor [tolerance=±5% resistance=10k package=THT]
  Rs1 = Resistor [tolerance=±5% resistance=100k package=THT]

nets:
  N1: J1.pin1, Rs.Pin_1
  N2: J1.pin2, A.D8
  N3: A.A0, toets1.Pin_3, toets1.Pin_4, Rs1.Pin_1
  N4: A.5V, R1.Pin_0
  N5: A.GND, Rs.Pin_0, Rs1.Pin_0
  N6: toets1.Pin_1, toets1.Pin_2, R1.Pin_1

notes:
  10K Ohm
  Bruin
  Zwart
  Oranje
  Goud
  100K Ohm
  Bruin
  Zwart
  Geel
  Goud
