# Fritzing sketch 19_fig_7 (saved by Fritzing 0.9.3b)
circuit board: 8.46667cm x 5.64444cm
breadboards: 1

parts:
  J1 = Piezo Speaker
  A = Arduino Uno (Rev3)
  toets1 = Pushbutton [package="[THT]"]
  R1 = Resistor [tolerance=±5% resistance=10k package=THT]
  Rs = Resistor [tolerance=±5% resistance=10k package=THT]
  Rs1 = Resistor [tolerance=±5% resistance=10k package=THT]
  toets2 = Pushbutton [package="[THT]"]
  R2 = Resistor [tolerance=±5% resistance=10k package=THT]
  R3 = Resistor [tolerance=±5% resistance=10k package=THT]
  toets3 = Pushbutton [package="[THT]"]
  R6 = Resistor [tolerance=±5% resistance=10k package=THT]
  R7 = Resistor [tolerance=±5% resistance=10k package=THT]
  R8 = Resistor [tolerance=±5% resistance=10k package=THT]
  toets4 = Pushbutton [package="[THT]"]
  R9 = Resistor [tolerance=±5% resistance=10k package=THT]
  R10 = Resistor [tolerance=±5% resistance=10k package=THT]
  R11 = Resistor [tolerance=±5% resistance=10k package=THT]
  R12 = Resistor [tolerance=±5% resistance=10k package=THT]
  R13 = Resistor [tolerance=±5% resistance=10k package=THT]
  R14 = Resistor [tolerance=±5% resistance=10k package=THT]
  toets5 = Pushbutton [package="[THT]"]
  toets6 = Pushbutton [package="[THT]"]
  R15 = Resistor [tolerance=±5% resistance=10k package=THT]
  R17 = Resistor [tolerance=±5% resistance=10k package=THT]
  R18 = Resistor [tolerance=±5% resistance=10k package=THT]
  toets7 = Pushbutton [package="[THT]"]
  R19 = Resistor [tolerance=±5% resistance=10k package=THT]
  R21 = Resistor [tolerance=±5% resistance=10k package=THT]
  R22 = Resistor [tolerance=±5% resistance=10k package=THT]
  R23 = Resistor [tolerance=±5% resistance=10k package=THT]

nets:
  N1: J1.pin1, Rs.Pin_1
  N2: J1.pin2, A.D8
  N3: A.A0, toets1.Pin_3, toets1.Pin_4, Rs1.Pin_1, toets2.Pin_3, toets2.Pin_4, toets3.Pin_3, toets3.Pin_4, toets4.Pin_3, toets4.Pin_4, toets5.Pin_3, toets5.Pin_4, toets6.Pin_3, toets6.Pin_4, toets7.Pin_3, toets7.Pin_4
  N4: A.5V, R1.Pin_0, R2.Pin_0, R6.Pin_0, R8.Pin_0, R9.Pin_0, R10.Pin_0, R11.Pin_0, R12.Pin_0, R13.Pin_0, R15.Pin_0
  N5: A.GND, Rs.Pin_0, Rs1.Pin_0
  N6: toets1.Pin_1, toets1.Pin_2, R1.Pin_1
  N7: toets2.Pin_1, toets2.Pin_2, R2.Pin_1, R3.Pin_1
  N8: toets3.Pin_1, toets3.Pin_2, R7.Pin_1, R8.Pin_1
  N9: toets4.Pin_1, toets4.Pin_2, R9.Pin_1, R10.Pin_1, R11.Pin_1, R12.Pin_1
  N10: R13.Pin_1, R14.Pin_0, R14.Pin_1, toets5.Pin_1, toets5.Pin_2
  N11: toets6.Pin_1, toets6.Pin_2, R18.Pin_1
  N12: R15.Pin_1, R17.Pin_0
  N13: R17.Pin_1, R18.Pin_0
  N14: toets7.Pin_1, toets7.Pin_2, R21.Pin_0
  N15: R19.Pin_1, R22.Pin_0
  N16: R21.Pin_1, R23.Pin_1
  N17: R22.Pin_1, R23.Pin_0
