# Fritzing sketch 1a_Blink (saved by Fritzing 0.9.3b)
circuit board: 8cm x 6cm
breadboards: 1

parts:
  LED1 = LED - 5mm [color="Red (633nm)" package="5 mm [THT]"]
  R1 = Resistor [tolerance=±5% resistance=1k package=THT]
  A1 = Arduino Uno (Rev3)

nets:
  N1: LED1.cathode, R1.Pin_0
  N2: LED1.anode, A1.D13/SCK
  N3: R1.Pin_1, A1.GND

notes:
  1000 Ohm
  Bruin
  Zwart
  Rood
  Goud
