# Fritzing sketch 1c_MeerKleurFadeMetFor (saved by Fritzing 0.9.3b)
circuit board: 8.46667cm x 5.64444cm
breadboards: 1

parts:
  LED1 = RGB LED (com. cathode, rgb) [package="5 mm [THT]"]
  RR = Resistor [tolerance=±5% resistance=1k package=THT]
  RG = Resistor [tolerance=±5% resistance=1k package=THT]
  RB = Resistor [tolerance=±5% resistance=1k package=THT]
  Part1 = Arduino Uno (Rev3)

nets:
  N1: LED1.red_anode, RR.Pin_0
  N2: LED1.common_cathode, Part1.GND
  N3: LED1.green_anode, RG.Pin_0
  N4: LED1.blue_anode, RB.Pin_0
  N5: RR.Pin_1, Part1.D11_PWM/MOSI
  N6: RG.Pin_1, Part1.D10_PWM/SS
  N7: RB.Pin_1, Part1.D9_PWM

notes:
  Langste pin naar GND
  1000 Ohm
  Bruin Zwart Rood Goud
  Gebruik pinnen met een golfje ~
  ervoor

// code stored in the sketch: 1c_MeerKleurFadeFor.ino
int pin_rood = 9;

void setup()
{
  pinMode(pin_rood, OUTPUT);
}

void loop()
{
  for (int i = 0; i!=256; ++i)
  {
    analogWrite(pin_rood, i);
    delay(30);
  }
}
