# Fritzing sketch 1d_ForNogEenKeer (saved by Fritzing 0.9.3b)
circuit board: 8.46667cm x 5.64444cm
breadboards: 1

parts:
  LED1 = LED - 5mm [color="Red (633nm)" package="5 mm [THT]"]
  LED2 = LED - 5mm [color="Red (633nm)" package="5 mm [THT]"]
  LED3 = LED - 5mm [color="Red (633nm)" package="5 mm [THT]"]
  LED4 = LED - 5mm [color="Red (633nm)" package="5 mm [THT]"]
  LED5 = LED - 5mm [color="Red (633nm)" package="5 mm [THT]"]
  LED6 = LED - 5mm [color="Red (633nm)" package="5 mm [THT]"]
  Part1 = Arduino Uno (Rev3)
  R1 = Resistor [tolerance=±5% resistance=1k package=THT]
  R2 = Resistor [tolerance=±5% resistance=1k package=THT]
  R3 = Resistor [tolerance=±5% resistance=1k package=THT]
  R4 = Resistor [tolerance=±5% resistance=1k package=THT]
  R5 = Resistor [tolerance=±5% resistance=1k package=THT]
  R6 = Resistor [tolerance=±5% resistance=1k package=THT]

nets:
  N1: LED1.cathode, R1.Pin_1
  N2: LED1.anode, Part1.D7
  N3: LED2.cathode, R2.Pin_1
  N4: LED2.anode, Part1.D6_PWM
  N5: LED3.cathode, R3.Pin_1
  N6: LED3.anode, Part1.D5_PWM
  N7: LED4.cathode, R4.Pin_1
  N8: LED4.anode, Part1.D4
  N9: LED5.cathode, R5.Pin_1
  N10: LED5.anode, Part1.D3_PWM
  N11: LED6.cathode, R6.Pin_1
  N12: LED6.anode, Part1.D2
  N13: Part1.GND, R1.Pin_0, R2.Pin_0, R3.Pin_0, R4.Pin_0, R5.Pin_0, R6.Pin_0

notes:
  1000 Ohm
  Bruin Zwart Rood Goud
