# Fritzing sketch 21_theremin_potmeters (saved by Fritzing 0.9.3b)
circuit board: 8.46667cm x 5.64444cm
breadboards: 1

parts:
  R1 = Rotary Potentiometer (Small) [maximum_resistance=100kΩ package=THT]
  R2 = Rotary Potentiometer (Small) [maximum_resistance=100kΩ package=THT]
  J1 = Piezo Speaker
  Part1 = Arduino Uno (Rev3)
  R4 = Resistor [tolerance=±5% resistance=10k package=THT]

nets:
  N1: R1.leg1, R2.leg1, Part1.5V
  N2: R1.wiper, Part1.A0
  N3: R1.leg2, R2.leg2, J1.pin1, Part1.GND
  N4: R2.wiper, Part1.A1
  N5: J1.pin2, R4.Pin_1
  N6: Part1.D5_PWM, R4.Pin_0

notes:
  Weerstand: 10 kOhm:
  bruin - zwart - oranje - goud
