# Fritzing sketch 22_theremin_ldr (saved by Fritzing 0.9.3b)
circuit board: 8.46667cm x 5.64444cm
breadboards: 1

parts:
  J1 = Piezo Speaker
  Part1 = Arduino Uno (Rev3)
  R4 = Resistor [tolerance=±5% resistance=10k package=THT]
  LDR1 = Photocell (LDR) [package=THT]
  LDR2 = Photocell (LDR) [package=THT]
  R7 = Resistor [tolerance=±5% resistance=10k package=THT]
  R8 = Resistor [tolerance=±5% resistance=10k package=THT]

nets:
  N1: J1.pin1, Part1.GND, R7.Pin_1, R8.Pin_1
  N2: J1.pin2, R4.Pin_1
  N3: Part1.A0, LDR1.pin_1, R7.Pin_0
  N4: Part1.A1, LDR2.pin_1, R8.Pin_0
  N5: Part1.D5_PWM, R4.Pin_0
  N6: Part1.5V, LDR1.pin_0, LDR2.pin_0

notes:
  Weestanden: 10kOhm
  bruin-zwart-oranje-goud
