# Fritzing sketch 23_theremin_infrarood (saved by Fritzing 0.9.3b)
circuit board: 8.46667cm x 5.64444cm
breadboards: 1

parts:
  J1 = Piezo Speaker
  Part1 = Arduino Uno (Rev3)
  R4 = Resistor [tolerance=±5% resistance=10k package=THT]
  R1 = Rotary Potentiometer (Small) [maximum_resistance=100kΩ package=THT]
  R2 = Rotary Potentiometer (Small) [maximum_resistance=100kΩ package=THT]

nets:
  N1: J1.pin1, Part1.GND, R1.leg2, R2.leg2
  N2: J1.pin2, R4.Pin_1
  N3: Part1.A0, R1.wiper
  N4: Part1.A1, R2.wiper
  N5: Part1.D5_PWM, R4.Pin_0
  N6: Part1.5V, R1.leg1, R2.leg1
