# Fritzing sketch 24_theremin_joystick (saved by Fritzing 0.9.3b)
circuit board: 8.46667cm x 5.64444cm
breadboards: 1

parts:
  J1 = Piezo Speaker
  Part1 = Arduino Uno (Rev3)
  R4 = Resistor [tolerance=±5% resistance=10k package=THT]
  Part2 = Thumb Joystick

nets:
  GND: J1.pin1, Part1.GND, Part2.GND
  N1: J1.pin2, R4.Pin_1
  N2: Part1.A0, Part2.VERT
  N3: Part1.A1, Part2.HORZ
  N4: Part1.D5_PWM, R4.Pin_0
  5V: Part1.5V, Part2.VCC

notes:
  Weerstand: 10 kOhm
  bruin-zwart-oranje-goud
