# Fritzing sketch 2_knop_if_else (saved by Fritzing 0.9.2b)
breadboards: 2

parts:
  LED1 = LED - 5mm [color="Red (633nm)" package="5 mm [THT]"]
  Part1 = Arduino Uno (Rev3)
  R1 = Resistor [tolerance=±5% resistance=1k package=THT]  # not connected
  S1 = Pushbutton [package="[THT]"]
  R2 = Resistor [tolerance=±5% resistance=10k package=THT]
  Part2 = Arduino Uno (Rev3)
  S2 = Pushbutton [package="[THT]"]
  R3 = Resistor [tolerance=±5% resistance=10k package=THT]
  LED2 = LED - 5mm [color="Red (633nm)" package="5 mm [THT]"]
  R4 = Resistor [tolerance=±5% resistance=1k package=THT]
  LED3 = LED - 5mm [color="Red (633nm)" package="5 mm [THT]"]
  R5 = Resistor [tolerance=±5% resistance=1k package=THT]

nets:
  N1: LED1.anode, Part1.D13/SCK
  N2: Part1.D12/MISO, LED3.anode
  N3: Part1.GND, R2.Pin_0, R5.Pin_1
  N4: Part1.D2, S1.Pin_1, S1.Pin_2, R2.Pin_1
  N5: Part1.5V, S1.Pin_3, S1.Pin_4
  N6: Part2.D13/SCK, LED2.anode
  N7: Part2.GND, R3.Pin_0, R4.Pin_1
  N8: Part2.D2, S2.Pin_1, S2.Pin_2, R3.Pin_1
  N9: Part2.5V, S2.Pin_3, S2.Pin_4
  N10: LED2.cathode, R4.Pin_0
  N11: LED3.cathode, R5.Pin_0
