# Fritzing sketch 3_meer_servo_motoren (saved by Fritzing 0.9.3b)
circuit board: 8.46667cm x 5.64444cm
breadboards: 4

parts:
  Part1 = Arduino Uno (Rev3)
  VCC1 = 4 x AAA Battery Mount
  J2 = Basic Servo
  S2 = Pushbutton [package="[THT]"]
  R2 = Resistor [tolerance=±5% resistance=10k package=THT]
  Part2 = Arduino Uno (Rev3)
  J4 = Basic Servo
  VCC2 = 4 x AAA Battery Mount
  Part3 = Arduino Uno (Rev3)
  J5 = Basic Servo
  J6 = Basic Servo
  VCC3 = 4 x AAA Battery Mount
  S6 = Pushbutton [package="[THT]"]
  R6 = Resistor [tolerance=±5% resistance=10k package=THT]
  Part4 = Arduino Uno (Rev3)
  J7 = Basic Servo
  J8 = Basic Servo
  VCC4 = 4 x AAA Battery Mount
  S7 = Pushbutton [package="[THT]"]
  S8 = Pushbutton [package="[THT]"]
  R7 = Resistor [tolerance=±5% resistance=10k package=THT]
  R8 = Resistor [tolerance=±5% resistance=10k package=THT]

nets:
  N1: Part1.A0, S2.Pin_1, S2.Pin_2, R2.Pin_0
  N2: Part1.D8, J2.pulse
  N3: Part1.5V, S2.Pin_3, S2.Pin_4
  GND: Part1.GND, VCC1.-, J2.gnd, R2.Pin_1
  N4: VCC1.+, J2.vcc
  N5: Part2.D8, J4.pulse
  GND_2: Part2.GND, J4.gnd, VCC2.-
  N6: J4.vcc, VCC2.+
  N7: Part3.A0, S6.Pin_1, S6.Pin_2, R6.Pin_0
  N8: Part3.D8, J6.pulse
  N9: Part3.D9_PWM, J5.pulse
  N10: Part3.5V, S6.Pin_3, S6.Pin_4
  GND_3: Part3.GND, J5.gnd, J6.gnd, VCC3.-, R6.Pin_1
  VCC: J5.vcc, J6.vcc, VCC3.+
  N11: Part4.A0, S8.Pin_1, S8.Pin_2, R7.Pin_0
  N12: Part4.A1, S7.Pin_1, S7.Pin_2, R8.Pin_0
  N13: Part4.D8, J7.pulse
  N14: Part4.D9_PWM, J8.pulse
  N15: Part4.5V, S7.Pin_3, S7.Pin_4, S8.Pin_3, S8.Pin_4
  GND_4: Part4.GND, J7.gnd, J8.gnd, VCC4.-, R7.Pin_1, R8.Pin_1
  VCC_2: J7.vcc, J8.vcc, VCC4.+

notes:
  10000 Ohm
  Bruin Zwart Oranje Goud

// code stored in the sketch: 3_meer_servo_motoren.ino

