# Fritzing sketch 3_servo_motor (saved by Fritzing 0.9.3b)
circuit board: 8.46667cm x 5.64444cm
circuit board: 8.46667cm x 5.64444cm

parts:
  A1 = Arduino Uno (Rev3)
  S1 = Basic Servo
  A2 = Arduino Uno (Rev3)
  S2 = Basic Servo
  R2 = Rotary Potentiometer (Small) [maximum_resistance=100kΩ package=THT]

nets:
  N1: A1.D9_PWM, S1.pulse
  GND: A1.GND, S1.gnd
  5V: A1.5V, S1.vcc
  N2: A2.A0, R2.wiper
  N3: A2.D9_PWM, S2.pulse
  GND_2: A2.GND, S2.gnd, R2.leg1
  5V_2: A2.5V, S2.vcc, R2.leg2
