# Fritzing sketch 4_FSR (saved by Fritzing 0.9.3b)
circuit board: 8.46667cm x 5.64444cm
circuit board: 8.46667cm x 5.64444cm
circuit board: 8.46667cm x 5.64444cm
breadboards: 2

parts:
  L1 = LED - 5mm [color="Red (633nm)" package="5 mm [THT]"]
  A3 = Arduino Uno (Rev3)
  RL1 = Resistor [tolerance=±5% resistance=1k package=THT]
  RF2 = Resistor [tolerance=±5% resistance=10k package=THT]
  FSR2 = Basic Force Sensing Resistor (FSR) [package=THT]
  A2 = Arduino Uno (Rev3)
  RF1 = Resistor [tolerance=±5% resistance=10k package=THT]
  FSR1 = Basic Force Sensing Resistor (FSR) [package=THT]
  A1 = Arduino Uno (Rev3)  # not connected

nets:
  N1: L1.cathode, RL1.Pin_0
  N2: L1.anode, A3.D13/SCK
  N3: A3.A0, RF2.Pin_1, FSR2.pin_1
  N4: A3.GND, RL1.Pin_1, RF2.Pin_0
  N5: A3.5V, FSR2.pin_0
  N6: A2.A0, RF1.Pin_1, FSR1.pin_1
  N7: A2.GND, RF1.Pin_0
  N8: A2.5V, FSR1.pin_0

notes:
  10000 Ohm
  Bruin
  Zwart
  Oranje
  Goud
  1000 Ohm
  Bruin
  Zwart
  Rood
  Goud
