# Fritzing sketch 4_FSR_met_servo (saved by Fritzing 0.9.3b)
circuit board: 8.46667cm x 5.64444cm
circuit board: 8.46667cm x 5.64444cm
breadboards: 2

parts:
  A2 = Arduino Uno (Rev3)
  R2 = Resistor [tolerance=±5% resistance=10k package=THT]
  FSR2 = Basic Force Sensing Resistor (FSR) [package=THT]
  A1 = Arduino Uno (Rev3)
  R1 = Resistor [tolerance=±5% resistance=10k package=THT]
  FSR1 = Basic Force Sensing Resistor (FSR) [package=THT]
  S2 = Basic Servo

nets:
  N1: A2.A0, R2.Pin_1, FSR2.pin_1
  N2: A2.D9_PWM, S2.pulse
  GND: A2.GND, R2.Pin_0, S2.gnd
  5V: A2.5V, FSR2.pin_0, S2.vcc
  N3: A1.A0, R1.Pin_1, FSR1.pin_1
  N4: A1.GND, R1.Pin_0
  N5: A1.5V, FSR1.pin_0

notes:
  10000 Ohm
  Bruin Zwart Oranje Goud
