# Fritzing sketch 5_dc_motor_met_transistor (saved by Fritzing 0.9.3b)
breadboards: 4

parts:
  Part1 = Arduino Uno (Rev3)
  S1 = Pushbutton [package="[THT]"]
  LED1 = LED - 5mm [color="Red (633nm)" package="5 mm [THT]"]
  R1 = Resistor [tolerance=±5% resistance=1k package=THT]
  VCC1 = 4 x AAA Battery Mount
  Part3 = Arduino Uno (Rev3)
  LED3 = LED - 5mm [color="Red (633nm)" package="5 mm [THT]"]
  R4 = Resistor [tolerance=±5% resistance=1k package=THT]
  VCC2 = 4 x AAA Battery Mount
  R5 = Resistor [tolerance=±5% resistance=1k package=THT]
  Q2 = NPN-Transistor [package="TO92 [THT]"]
  Part5 = Arduino Uno (Rev3)
  R6 = Resistor [tolerance=±5% resistance=1k package=THT]
  Q3 = NPN-Transistor [package="TO92 [THT]"]
  VCC3 = 4 x AAA Battery Mount
  M1 = DC Motor
  D1 = Rectifier Diode [part_number=1N4001 package="300 mil [THT]"]
  C1 = Electrolytic Capacitor [capacitance=1µF package="100 mil [THT, electrolytic]"]
  Part6 = Arduino Uno (Rev3)
  VCC4 = 4 x AAA Battery Mount
  M2 = DC Motor
  D2 = Rectifier Diode [part_number=1N4001 package="300 mil [THT]"]
  C2 = Electrolytic Capacitor [capacitance=1µF package="100 mil [THT, electrolytic]"]
  S2 = Pushbutton [package="[THT]"]

nets:
  N1: Part1.GND, R1.Pin_1, VCC1.-
  N2: S1.Pin_1, S1.Pin_2, LED1.anode
  N3: S1.Pin_3, S1.Pin_4, VCC1.+
  N4: LED1.cathode, R1.Pin_0
  N5: Part3.D13/SCK, R5.Pin_1
  N6: Part3.GND, R4.Pin_1, VCC2.-
  N7: LED3.cathode, R4.Pin_0
  N8: LED3.anode, Q2.C
  N9: VCC2.+, Q2.E
  N10: R5.Pin_0, Q2.B
  N11: Part5.D13/SCK, R6.Pin_1
  N12: Part5.GND, VCC3.-, M1.pin_2, D1.anode, C1.-
  N13: R6.Pin_0, Q3.B
  N14: Q3.E, VCC3.+, C1.+
  N15: Q3.C, M1.pin_1, D1.cathode
  N16: Part6.GND, VCC4.-, M2.pin_2, D2.anode, C2.-
  N17: VCC4.+, C2.+, S2.Pin_3, S2.Pin_4
  N18: M2.pin_1, D2.cathode, S2.Pin_1, S2.Pin_2

notes:
  1000 Ohm
  bruin zwart
  rood
  goud
  Allebei
  1000 Ohm bruin
  zwart
  rood
  goud
  1000 Ohm
  witte punt aan GND
  witte streep aan plus
