# Fritzing sketch 6_muziek_tone (saved by Fritzing 0.9.3b)
breadboards: 1

parts:
  J1 = Piezo Speaker
  Part1 = Arduino Uno (Rev3)
  R1 = Resistor [tolerance=±5% resistance=10k package=THT]

nets:
  N1: J1.pin1, Part1.GND
  N2: J1.pin2, R1.Pin_0
  N3: Part1.D8, R1.Pin_1

notes:
  10.000 Ohm
  10 kOhm
  Bruin-Zwart-Oranje-Goud
