# Fritzing sketch 7_dc_motor_met_relais (saved by Fritzing 0.9.3b)
breadboards: 4

parts:
  Part3 = Arduino Uno (Rev3)
  LED3 = LED - 5mm [color="Red (633nm)" package="5 mm [THT]"]
  R4 = Resistor [tolerance=±5% resistance=1k package=THT]
  R5 = Resistor [tolerance=±5% resistance=1k package=THT]
  Q2 = NPN-Transistor [package="TO92 [THT]"]
  Part4 = Arduino Uno (Rev3)
  R6 = Resistor [tolerance=±5% resistance=1k package=THT]
  Q3 = NPN-Transistor [package="TO92 [THT]"]
  U1 = mystery part, 8 pins [chip_label=Relais]
  D1 = Rectifier Diode [part_number=1N4001 package="300 mil [THT]"]
  Part5 = Arduino Uno (Rev3)
  R7 = Resistor [tolerance=±5% resistance=1k package=THT]
  Q4 = NPN-Transistor [package="TO92 [THT]"]
  U2 = mystery part, 8 pins [chip_label=Relais]
  D2 = Rectifier Diode [part_number=1N4001 package="300 mil [THT]"]
  LED4 = LED - 5mm [color="Red (633nm)" package="5 mm [THT]"]
  LED5 = LED - 5mm [color="Green (555nm)" package="5 mm [THT]"]
  R8 = Resistor [tolerance=±5% resistance=1k package=THT]
  Part6 = Arduino Uno (Rev3)
  R10 = Resistor [tolerance=±5% resistance=1k package=THT]
  Q5 = NPN-Transistor [package="TO92 [THT]"]
  U3 = mystery part, 8 pins [chip_label=Relais]
  D3 = Rectifier Diode [part_number=1N4001 package="300 mil [THT]"]
  M1 = DC Motor
  VCC1 = 4 x AAA Battery Mount

nets:
  N1: Part3.D13/SCK, R5.Pin_1
  N2: Part3.5V, Q2.E
  N3: Part3.GND, R4.Pin_1
  N4: LED3.cathode, R4.Pin_0
  N5: LED3.anode, Q2.C
  N6: R5.Pin_0, Q2.B
  N7: Part4.D13/SCK, R6.Pin_1
  N8: Part4.5V, Q3.E
  N9: Part4.GND, U1.pin1, D1.anode
  N10: R6.Pin_0, Q3.B
  N11: Q3.C, U1.pin8, D1.cathode
  N12: Part5.D13/SCK, R7.Pin_1
  N13: Part5.5V, Q4.E, U2.pin7
  N14: Part5.GND, U2.pin1, D2.anode, R8.Pin_1
  N15: R7.Pin_0, Q4.B
  N16: Q4.C, U2.pin8, D2.cathode
  N17: U2.pin5, LED5.anode
  N18: U2.pin6, LED4.anode
  N19: LED4.cathode, LED5.cathode, R8.Pin_0
  N20: Part6.D13/SCK, R10.Pin_1
  N21: Part6.5V, Q5.E
  N22: Part6.GND, U3.pin1, D3.anode
  N23: R10.Pin_0, Q5.B
  N24: Q5.C, U3.pin8, D3.cathode
  N25: U3.pin2, M1.pin_2
  N26: U3.pin3, U3.pin5, VCC1.-
  N27: U3.pin4, U3.pin6, VCC1.+
  N28: U3.pin7, M1.pin_1

notes:
  Allebei
  1000 Ohm bruin
  zwart
  rood
  goud
  1000 Ohm bruin
  zwart
  rood
  goud
  witte streep aan plus (bovenkant)
