# Fritzing sketch 8_infrarood_sensor_obstakel_ontwijkend_object (saved by Fritzing 0.9.3b)
breadboards: 7

parts:
  Part3 = Arduino Uno (Rev3)
  LED3 = LED - 5mm [color="Red (633nm)" package="5 mm [THT]"]
  R4 = Resistor [tolerance=±5% resistance=1k package=THT]
  R5 = Resistor [tolerance=±5% resistance=1k package=THT]
  Q2 = NPN-Transistor [package="TO92 [THT]"]
  Part4 = Arduino Uno (Rev3)
  R6 = Resistor [tolerance=±5% resistance=1k package=THT]
  Q3 = NPN-Transistor [package="TO92 [THT]"]
  U1 = mystery part, 8 pins [chip_label=Relais]
  D1 = Rectifier Diode [part_number=1N4001 package="300 mil [THT]"]
  Part5 = Arduino Uno (Rev3)
  R7 = Resistor [tolerance=±5% resistance=1k package=THT]
  Q4 = NPN-Transistor [package="TO92 [THT]"]
  U2 = mystery part, 8 pins [chip_label=Relais]
  D2 = Rectifier Diode [part_number=1N4001 package="300 mil [THT]"]
  LED4 = LED - 5mm [color="Red (633nm)" package="5 mm [THT]"]
  LED5 = LED - 5mm [color="Green (555nm)" package="5 mm [THT]"]
  R8 = Resistor [tolerance=±5% resistance=1k package=THT]
  Part6 = Arduino Uno (Rev3)
  R10 = Resistor [tolerance=±5% resistance=1k package=THT]
  Q5 = NPN-Transistor [package="TO92 [THT]"]
  U3 = mystery part, 8 pins [chip_label=Relais]
  D3 = Rectifier Diode [part_number=1N4001 package="300 mil [THT]"]
  M1 = DC Motor
  VCC1 = 4 x AAA Battery Mount
  Part7 = Arduino Uno (Rev3)
  U4 = mystery part, 8 pins [chip_label=Relais]
  D4 = Rectifier Diode [part_number=1N4001 package="300 mil [THT]"]
  M2 = DC Motor
  VCC2 = 4 x AAA Battery Mount
  R11 = Resistor [tolerance=±5% resistance=1k package=THT]
  Q6 = NPN-Transistor [package="TO92 [THT]"]
  M3 = DC Motor
  Part8 = Arduino Uno (Rev3)
  U5 = mystery part, 8 pins [chip_label=Relais]
  D5 = Rectifier Diode [part_number=1N4001 package="300 mil [THT]"]
  M4 = DC Motor
  M5 = DC Motor
  VCC3 = 4 x AAA Battery Mount
  R12 = Resistor [tolerance=±5% resistance=1k package=THT]
  Q7 = NPN-Transistor [package="TO92 [THT]"]
  J1 = Infrared Proximity Sensor
  Part9 = Arduino Uno (Rev3)
  J2 = Infrared Proximity Sensor

nets:
  N1: Part3.D13/SCK, R5.Pin_1
  N2: Part3.5V, Q2.E
  N3: Part3.GND, R4.Pin_1
  N4: LED3.cathode, R4.Pin_0
  N5: LED3.anode, Q2.C
  N6: R5.Pin_0, Q2.B
  N7: Part4.D13/SCK, R6.Pin_1
  N8: Part4.5V, Q3.E
  N9: Part4.GND, U1.pin1, D1.anode
  N10: R6.Pin_0, Q3.B
  N11: Q3.C, U1.pin8, D1.cathode
  N12: Part5.D13/SCK, R7.Pin_1
  N13: Part5.5V, Q4.E, U2.pin7
  N14: Part5.GND, U2.pin1, D2.anode, R8.Pin_1
  N15: R7.Pin_0, Q4.B
  N16: Q4.C, U2.pin8, D2.cathode
  N17: U2.pin5, LED5.anode
  N18: U2.pin6, LED4.anode
  N19: LED4.cathode, LED5.cathode, R8.Pin_0
  N20: Part6.D13/SCK, R10.Pin_1
  N21: Part6.5V, Q5.E
  N22: Part6.GND, U3.pin1, D3.anode
  N23: R10.Pin_0, Q5.B
  N24: Q5.C, U3.pin8, D3.cathode
  N25: U3.pin2, M1.pin_2
  N26: U3.pin3, U3.pin5, VCC1.-
  N27: U3.pin4, U3.pin6, VCC1.+
  N28: U3.pin7, M1.pin_1
  N29: Part7.D13/SCK, R11.Pin_1
  N30: Part7.5V, Q6.E
  N31: Part7.GND, U4.pin1, D4.anode
  N32: U4.pin2, M2.pin_2
  N33: U4.pin3, U4.pin5, VCC2.-, M3.pin_1
  N34: U4.pin4, U4.pin6, VCC2.+, M3.pin_2
  N35: U4.pin7, M2.pin_1
  N36: U4.pin8, D4.cathode, Q6.C
  N37: R11.Pin_0, Q6.B
  N38: Part8.A0, J1.Vout
  N39: Part8.D13/SCK, R12.Pin_1
  5V: Part8.5V, Q7.E, J1.Vcc
  GND: Part8.GND, U5.pin1, D5.anode, J1.GND
  N40: U5.pin2, M4.pin_2
  N41: U5.pin3, U5.pin5, M5.pin_1, VCC3.-
  N42: U5.pin4, U5.pin6, M5.pin_2, VCC3.+
  N43: U5.pin7, M4.pin_1
  N44: U5.pin8, D5.cathode, Q7.C
  N45: R12.Pin_0, Q7.B
  N46: Part9.A0, J2.Vout
  5V_2: Part9.5V, J2.Vcc
  GND_2: Part9.GND, J2.GND

notes:
  Allebei
  1000 Ohm bruin
  zwart
  rood
  goud
  1000 Ohm bruin
  zwart
  rood
  goud
  witte streep aan plus (bovenkant)
