# Fritzing sketch 9_LDR (saved by Fritzing 0.9.3b)
circuit board: 8.46667cm x 5.64444cm
circuit board: 8.46667cm x 5.64444cm
circuit board: 8.46667cm x 5.64444cm
breadboards: 2

parts:
  L1 = LED - 5mm [color="Red (633nm)" package="5 mm [THT]"]
  A3 = Arduino Uno (Rev3)
  R1 = Resistor [tolerance=±5% resistance=1k package=THT]
  RL2 = Resistor [tolerance=±5% resistance=10k package=THT]
  A2 = Arduino Uno (Rev3)
  A1 = Arduino Uno (Rev3)  # not connected
  LDR1 = Photocell (LDR) [package=THT]
  LDR2 = Photocell (LDR) [package=THT]
  RL1 = Resistor [tolerance=±5% resistance=10k package=THT]

nets:
  N1: L1.cathode, R1.Pin_0
  N2: L1.anode, A3.D13/SCK
  N3: A3.A0, RL2.Pin_1, LDR2.pin_1
  N4: A3.GND, R1.Pin_1, RL2.Pin_0
  N5: A3.5V, LDR2.pin_0
  N6: A2.A0, LDR1.pin_1, RL1.Pin_1
  N7: A2.GND, RL1.Pin_0
  N8: A2.5V, LDR1.pin_0

notes:
  10000 Ohm
  Bruin
  Zwart
  Oranje
  Goud
  1000 Ohm
  Bruin
  Zwart
  Rood
  Goud
