# Fritzing sketch CapacitieveSensor1 (saved by Fritzing 0.9.3b)
circuit board: 8.46667cm x 5.64444cm
breadboards: 1

parts:
  Part1 = Arduino Uno (Rev3)
  R_hulp = Resistor [tolerance=±5% resistance=1M package=THT]
  R_sensor = Resistor [tolerance=±5% resistance=1k package=THT]
  R_knop = Resistor [tolerance=±5% resistance=0 package=THT]

nets:
  N1: Part1.D2, R_hulp.Pin_0
  N2: Part1.D4, R_sensor.Pin_1
  N3: R_hulp.Pin_1, R_sensor.Pin_0, R_knop.Pin_0
