# Fritzing sketch CapacitieveSensor2 (saved by Fritzing 0.9.3b)
circuit board: 8.46667cm x 5.64444cm
breadboards: 1

parts:
  Part1 = Arduino Uno (Rev3)
  R_hulp_1 = Resistor [tolerance=±5% resistance=1M package=THT]
  R_sensor_1 = Resistor [tolerance=±5% resistance=1k package=THT]
  R_knop_1 = Resistor [tolerance=±5% resistance=0 package=THT]
  R_hulp_2 = Resistor [tolerance=±5% resistance=1M package=THT]
  R_sensor_2 = Resistor [tolerance=±5% resistance=1k package=THT]
  R_knop_2 = Resistor [tolerance=±5% resistance=0 package=THT]

nets:
  N1: Part1.D8, R_sensor_2.Pin_1
  N2: Part1.D2, R_hulp_1.Pin_0
  N3: Part1.D4, R_sensor_1.Pin_1
  N4: Part1.D6_PWM, R_hulp_2.Pin_0
  N5: R_hulp_1.Pin_1, R_sensor_1.Pin_0, R_knop_1.Pin_0
  N6: R_hulp_2.Pin_1, R_sensor_2.Pin_0, R_knop_2.Pin_0
