# Fritzing sketch CapacitieveSensor2_3 (saved by Fritzing 0.9.3b)
circuit board: 8.46667cm x 5.64444cm
breadboards: 1

parts:
  Part1 = Arduino Uno (Rev3)
  R_hulp_1 = Resistor [tolerance=±5% resistance=1M package=THT]
  R_sensor_1 = Resistor [tolerance=±5% resistance=1k package=THT]
  R_knop_1 = Resistor [tolerance=±5% resistance=0 package=THT]
  R_hulp_2 = Resistor [tolerance=±5% resistance=1M package=THT]
  R_sensor_2 = Resistor [tolerance=±5% resistance=1k package=THT]
  R_knop_2 = Resistor [tolerance=±5% resistance=0 package=THT]
  R1 = Resistor [tolerance=±5% resistance=1k package=THT]
  LED1 = LED - 5mm [color="Red (633nm)" package="5 mm [THT]"]
  R2 = Resistor [tolerance=±5% resistance=1k package=THT]
  LED2 = LED - 5mm [color="Red (633nm)" package="5 mm [THT]"]
  R3 = Resistor [tolerance=±5% resistance=1k package=THT]
  LED3 = LED - 5mm [color="Red (633nm)" package="5 mm [THT]"]

nets:
  N1: Part1.D8, R_sensor_2.Pin_1
  N2: Part1.D11_PWM/MOSI, LED1.anode
  N3: Part1.D12/MISO, LED2.anode
  N4: Part1.D13/SCK, LED3.anode
  N5: Part1.GND, R1.Pin_1, R2.Pin_1, R3.Pin_1
  N6: Part1.D2, R_hulp_1.Pin_0
  N7: Part1.D4, R_sensor_1.Pin_1
  N8: Part1.D6_PWM, R_hulp_2.Pin_0
  N9: R_hulp_1.Pin_1, R_sensor_1.Pin_0, R_knop_1.Pin_0
  N10: R_hulp_2.Pin_1, R_sensor_2.Pin_0, R_knop_2.Pin_0
  N11: R1.Pin_0, LED1.cathode
  N12: R2.Pin_0, LED2.cathode
  N13: R3.Pin_0, LED3.cathode
