# Fritzing sketch SerialCommunication (saved by Fritzing 0.9.0b)

parts:
  Part1 = Arduino Uno (Rev3)
  Part2 = Arduino Uno (Rev3)
  Part3 = Arduino Uno (Rev3)
  Part4 = Arduino Uno (Rev3)

nets:
  N1: Part1.D0/RX, Part4.D11_PWM/MOSI
  N2: Part1.D1/TX, Part2.D0/RX
  N3: Part2.D1/TX, Part3.D0/RX
  N4: Part3.D1/TX, Part4.D10_PWM/SS

notes:
  void setup()
  {
  Serial.begin(9600);
  }
  void loop()
  {
  while(Serial.available())
  {
  Serial.write(Serial.read());
  }
  }
  #include <SoftwareSerial.h>
  SoftwareSerial mySerial(10, 11); // RX, TX
  void setup()
  {
  Serial.begin(9600);
  mySerial.begin(9600);
  }
  void loop() // run over and over
  {
  bool changed = false;
  while (mySerial.available())
  {
  Serial.write(mySerial.read());
  changed = true;
  }
  if (changed) { Serial.print('\n'); }
  while (Serial.available()){
  mySerial.write(Serial.read());
  }
  }
