# Fritzing sketch DcMotorMetTransistor (saved by Fritzing 0.9.3b)
breadboards: 2

parts:
  M2 = DC Motor
  VCC1 = 4 x AAA Battery Mount
  M1 = DC Motor
  M3 = DC Motor
  VCC3 = 4 x AAA Battery Mount
  S1 = Pushbutton [package=THT]
  VCC4 = 4 x AAA Battery Mount
  Q4 = NPN-Transistor [package="TO92 [THT]"]
  M4 = DC Motor
  M5 = DC Motor
  VCC5 = 4 x AAA Battery Mount
  Q5 = NPN-Transistor [package="TO92 [THT]"]
  A4 = Arduino Uno (Rev3)
  A5 = Arduino Uno (Rev3)
  A3 = Arduino Uno (Rev3)  # not connected
  A2 = Arduino Uno (Rev3)
  D2 = Rectifier Diode [part_number=1N4001 package="300 mil [THT]"]
  R5 = Resistor [tolerance=±5% resistance=4.7k package=THT]
  M6 = DC Motor
  D6 = Rectifier Diode [part_number=1N4001 package="300 mil [THT]"]
  VCC6 = 4 x AAA Battery Mount
  part = 4 x AAA Battery Mount  # not connected

nets:
  N1: M2.pin_1, A2.GND
  N2: M2.pin_2, A2.A0
  N3: VCC1.-, M1.pin_1
  N4: VCC1.+, M1.pin_2
  N5: M3.pin_1, VCC3.-
  N6: M3.pin_2, S1.leg0
  N7: VCC3.+, S1.leg1
  N8: VCC4.-, Q4.E, A4.GND
  N9: VCC4.+, M4.pin_1
  N10: Q4.B, A4.D2
  N11: Q4.C, M4.pin_2
  N12: M5.pin_1, VCC5.+, D2.cathode
  N13: M5.pin_2, Q5.C, D2.anode
  N14: VCC5.-, Q5.E, A5.GND
  N15: Q5.B, R5.Pin_0
  N16: A5.D2, R5.Pin_1
  N17: M6.pin_1, D6.cathode, VCC6.+
  N18: M6.pin_2, D6.anode, VCC6.-

notes:
  Naief
  NIET DOEN!
  5 V
  Correct
  'Arduino drukt
  op de knop'
  Naief
  NIET DOEN
  E B C
  • C: Collector ('kollektor'): naar vermogensbron
  • B: Base ('bees'): aansturing door Arduino
  • E: Emittor ('iemittor'): naar Aarde
  Smoordiode
  Weerstand om kortsluiting te voorkomen
