# Fritzing sketch LdrEnLed (saved by Fritzing 0.9.0b)
breadboards: 1

parts:
  S3 = Photocell (LDR) [package=THT]
  R5 = Resistor [tolerance=±5% resistance=1k package=THT]  # not connected
  Part2 = Arduino Uno (Rev3)
  R6 = Resistor [tolerance=±5% resistance=1k package=THT]  # not connected
  LED1 = LED - 5mm [color="Red (633nm)" package="5 mm [THT]"]

nets:
  N1: S3.pin_0, Part2.5V
  N2: S3.pin_1, Part2.A0
  N3: Part2.GND, LED1.cathode
