# Fritzing sketch Laser (saved by Fritzing 0.9.3b)
circuit board: 8cm x 6cm
breadboards: 2

parts:
  Laser = LED - 5mm [color="White (8000K)" package="5 mm [THT]"]
  R1 = Resistor [tolerance=±5% resistance=40 package=THT]
  A1 = Arduino Uno (Rev3)
  AR = Arduino Uno (Rev3)
  LR1 = LED - 5mm [color="Red (633nm)" package="5 mm [THT]"]
  RR1 = Resistor [tolerance=±5% resistance=1k package=THT]
  SR1 = Photocell (LDR) [package=THT]
  RR2 = Resistor [tolerance=±5% resistance=10k package=THT]

nets:
  N1: Laser.cathode, R1.Pin_0
  N2: Laser.anode, A1.D13/SCK
  N3: R1.Pin_1, A1.GND
  N4: AR.A0, SR1.pin_0, RR2.Pin_0
  N5: AR.D13/SCK, LR1.anode
  N6: AR.GND, RR1.Pin_1, RR2.Pin_1
  N7: AR.5V, SR1.pin_1
  N8: LR1.cathode, RR1.Pin_0

notes:
  40 Ohm
  Geel
  Zwart
  Zwart
  Goud
  Laser
