# Fritzing sketch Nokia5110SparkfunLogicLevelConverters (saved by Fritzing 0.9.2b)
breadboards: 1

parts:
  Nokia_5110_LCD_Module1 = Nokia5110LCDModule
  Part1 = Logic Level Converter
  Part2 = Logic Level Converter
  Part3 = Arduino Uno (Rev3)

nets:
  N1: Nokia_5110_LCD_Module1.Vcc, Part2.TX_LV
  N2: Nokia_5110_LCD_Module1.Grnd, Part2.RX_LV
  N3: Nokia_5110_LCD_Module1.SCE, Part2.RX2_LV
  N4: Nokia_5110_LCD_Module1.RST, Part2.TX2_LV
  N5: Nokia_5110_LCD_Module1.D/C, Part1.TX_LV
  N6: Nokia_5110_LCD_Module1.6_DN_(MOSI), Part1.LV, Part2.LV, Part3.3V3
  N7: Nokia_5110_LCD_Module1.SCLK, Part1.RX_LV
  GND: Nokia_5110_LCD_Module1.LED, Part1.GND, Part2.GND, Part3.GND
  N8: Part1.TX_HV, Part3.D6_PWM
  N9: Part1.RX_HV, Part3.D7
  N10: Part1.HV, Part2.HV, Part3.5V
  N11: Part2.TX_HV, Part3.D2
  N12: Part2.RX_HV, Part3.D3_PWM
  N13: Part2.RX2_HV, Part3.D4
  N14: Part2.TX2_HV, Part3.D5_PWM

notes:
  From left to right:
  RST, CE, DC, Din, Clk, Vcc BL Gnd
  RST = Reset
  CE = Chip Enable
  DC = Data / Command
  Din = Data in
  Clk = Clock signal
  Vcc = Power 3.3v DC
  BL = Backlight
  Gnd = Ground 0v
  RST - pulse LOW to reset
  CE - LOW to enable
  DC - HIGH for data, LOW for commands

custom parts:
  : Nokia 5110 LCD with 8 pin. It's a 45mm*45mm module part. Description: The Nokia 5110 is a basic graphic LCD screen for lots of applications. It was originally intended for as a cell phone screen. This one is mounted on an easy to solder PCB. It uses the PCD8544 controller. The PCD8544 is a low power CMOS LCD controller/driver, designed to drive a graphic display of 48 rows and 84 columns. All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
