# Fritzing sketch 3_servo_motor (saved by Fritzing 0.9.2b)

parts:
  Part2 = Arduino Uno (Rev3)
  J1 = Basic Servo
  Part3 = Arduino Uno (Rev3)
  J2 = Basic Servo
  R2 = Rotary Potentiometer (Small) [maximum_resistance=100kΩ package=THT]

nets:
  N1: Part2.D9_PWM, J1.pulse
  5V: Part2.5V, J1.vcc
  GND: Part2.GND, J1.gnd
  N2: Part3.A0, R2.wiper
  N3: Part3.D9_PWM, J2.pulse
  5V_2: Part3.5V, J2.vcc, R2.leg2
  GND_2: Part3.GND, J2.gnd, R2.leg1
