# Fritzing sketch Piano_een_pin (saved by Fritzing 0.9.3b)
circuit board: 8.46667cm x 5.64444cm
breadboards: 1

parts:
  J1 = Piezo Speaker
  A = Arduino Uno (Rev3)
  Rs = Resistor [tolerance=±5% resistance=10k package=THT]
  toets1 = Pushbutton [package="[THT]"]
  R1 = Resistor [tolerance=±5% resistance=330 package=THT]
  toets2 = Pushbutton [package="[THT]"]
  R2 = Resistor [tolerance=±5% resistance=1k package=THT]
  toets3 = Pushbutton [package="[THT]"]
  R3 = Resistor [tolerance=±5% resistance=10k package=THT]
  Rt = Resistor [tolerance=±5% resistance=10k package=THT]

nets:
  N1: J1.pin1, Rs.Pin_1
  N2: J1.pin2, A.D8
  N3: A.A0, R1.Pin_1, R2.Pin_1, R3.Pin_1, Rt.Pin_0
  N4: A.5V, toets1.Pin_3, toets1.Pin_4, toets2.Pin_3, toets2.Pin_4, toets3.Pin_3, toets3.Pin_4
  N5: A.GND, Rs.Pin_0, Rt.Pin_1
  N6: toets1.Pin_1, toets1.Pin_2, R1.Pin_0
  N7: toets2.Pin_1, toets2.Pin_2, R2.Pin_0
  N8: toets3.Pin_1, toets3.Pin_2, R3.Pin_0

notes:
  10K Ohm
  Bruin
  Zwart
  Oranje
  Goud
  330 Ohm
  Oranje
  Oranje
  Bruin
  Goud
  1K Ohm
  Bruin
  Zwart
  Rood
  Goud
  1K Ohm
  Bruin
  Zwart
  Oranje
  Goud
