# Fritzing sketch Piano_parallel (saved by Fritzing 0.9.3b)
breadboards: 1

parts:
  J1 = Piezo Speaker
  Part1 = Arduino Uno (Rev3)
  R1 = Resistor [tolerance=±5% resistance=10k package=THT]
  S1 = Pushbutton [package="[THT]"]
  S2 = Pushbutton [package="[THT]"]
  S3 = Pushbutton [package="[THT]"]
  R2 = Resistor [tolerance=±5% resistance=10k package=THT]
  R3 = Resistor [tolerance=±5% resistance=10k package=THT]  # not connected
  R4 = Resistor [tolerance=±5% resistance=10k package=THT]

nets:
  N1: J1.pin2, R1.Pin_0, R1.Pin_1
  N2: Part1.A0, S3.Pin_1, S3.Pin_2, R2.Pin_0
  N3: Part1.A1, S2.Pin_1, S2.Pin_2
  N4: Part1.A2, S1.Pin_1, S1.Pin_2, R4.Pin_0
  N5: S1.Pin_3, S1.Pin_4, S2.Pin_3, S2.Pin_4, S3.Pin_3, S3.Pin_4
  N6: R2.Pin_1, R4.Pin_1

notes:
  10K Ohm
  Bruin
  Zwart
  Oranje
  Goud
