# Fritzing sketch Piano_serie (saved by Fritzing 0.9.3b)
circuit board: 8.46667cm x 5.64444cm
breadboards: 1

parts:
  J1 = Piezo Speaker
  A = Arduino Uno (Rev3)
  Rs = Resistor [tolerance=±5% resistance=10k package=THT]
  toets1 = Pushbutton [package="[THT]"]
  toets2 = Pushbutton [package="[THT]"]
  toets3 = Pushbutton [package="[THT]"]
  R1 = Resistor [tolerance=±5% resistance=1k package=THT]
  R2 = Resistor [tolerance=±5% resistance=1k package=THT]
  R3 = Resistor [tolerance=±5% resistance=10k package=THT]

nets:
  N1: J1.pin1, Rs.Pin_1
  N2: J1.pin2, A.D8
  N3: A.A0, toets1.Pin_1, toets1.Pin_2, R1.Pin_0
  N4: A.A1, toets2.Pin_1, toets2.Pin_2, R2.Pin_0
  N5: A.A2, toets3.Pin_1, toets3.Pin_2, R3.Pin_0
  N6: A.5V, toets1.Pin_3, toets1.Pin_4
  N7: A.GND, Rs.Pin_0, R3.Pin_1
  N8: toets2.Pin_3, toets2.Pin_4, R1.Pin_1
  N9: toets3.Pin_3, toets3.Pin_4, R2.Pin_1

notes:
  10K Ohm
  Bruin
  Zwart
  Oranje
  Goud
  1K Ohm
  Bruin
  Zwart
  Rood
  Goud
