# Fritzing sketch Potmeter (saved by Fritzing 0.9.2b)
breadboards: 2

parts:
  LED1 = LED - 5mm [color="Red (633nm)" package="5 mm [THT]"]
  Part1 = Arduino Uno (Rev3)
  R1 = Resistor [tolerance=±5% resistance=1k package=THT]  # not connected
  R4 = Rotary Potentiometer (Small) [maximum_resistance=100kΩ package=THT]
  Part2 = Arduino Uno (Rev3)
  R6 = Rotary Potentiometer (Small) [maximum_resistance=100kΩ package=THT]

nets:
  N1: LED1.anode, Part1.D9_PWM
  N2: Part1.A0, R4.wiper
  N3: Part1.GND, R4.leg2
  N4: Part1.5V, R4.leg1
  N5: Part2.A0, R6.wiper
  N6: Part2.GND, R6.leg2
  N7: Part2.5V, R6.leg1
