# Fritzing sketch PiezoEnLdr (saved by Fritzing 0.9.0b)
breadboards: 1

parts:
  J1 = Piezo Speaker
  Part1 = Arduino Uno (Rev3)
  R1 = Resistor [tolerance=±5% resistance=1k package=THT]
  S5 = Photocell (LDR) [package=THT]
  R7 = Resistor [tolerance=±5% resistance=1k package=THT]

nets:
  N1: J1.pin1, Part1.GND, R7.Pin_1
  N2: J1.pin2, R1.Pin_0
  N3: Part1.A0, S5.pin_1, R7.Pin_0
  N4: Part1.D8, R1.Pin_1
  N5: Part1.5V, S5.pin_0
