# Fritzing sketch Theremin_infrarood (saved by Fritzing 0.9.3b)
circuit board: 8.46667cm x 5.64444cm
breadboards: 1

parts:
  A = Arduino Uno (Rev3)
  S = Infrared Proximity Sensor
  P = Piezo Speaker

nets:
  N1: A.A0, S.Vout
  N2: A.D8, P.pin2
  GND: A.GND, S.GND, P.pin1
  5V: A.5V, S.Vcc

// code stored in the sketch: Theremin_infrarood.ino
const int sensor_pin = A0;
const int piezo_pin = 8;

void setup()
{
  pinMode(piezo_pin, OUTPUT);
  pinMode(sensor_pin, INPUT); 
  Serial.begin(9600);
}

void loop()
{
  const int sensor_waarde = analogRead(sensor_pin);
  Serial.println(sensor_waarde);
  tone(piezo_pin, sensor_waarde, 10);
  delay(10);
}
