# Fritzing sketch ArduinoCourseConnect7SegmentDisplay (saved by Fritzing 0.8.5b)
breadboards: 1

parts:
  R1 = Resistor [tolerance=±5% resistance=220 package=THT]
  R2 = Resistor [tolerance=±5% resistance=220 package=THT]
  R3 = Resistor [tolerance=±5% resistance=220 package=THT]
  R4 = Resistor [tolerance=±5% resistance=220 package=THT]
  R5 = Resistor [tolerance=±5% resistance=220 package=THT]
  R6 = Resistor [tolerance=±5% resistance=220 package=THT]
  R7 = Resistor [tolerance=±5% resistance=220 package=THT]
  R8 = Resistor [tolerance=±5% resistance=220 package=THT]
  IC1 = IC, DIP package, 14 pins [chip_label=IC]
  Part1 = Arduino Uno (Rev3)

nets:
  N1: R1.Pin_0, Part1.D3_PWM
  N2: R1.Pin_1, IC1.pin2
  N3: R2.Pin_0, Part1.D2
  N4: R2.Pin_1, IC1.pin1
  N5: R3.Pin_0, Part1.D4
  N6: R3.Pin_1, IC1.pin7
  N7: R4.Pin_0, IC1.pin8
  N8: R4.Pin_1, Part1.D5_PWM
  N9: R5.Pin_0, IC1.pin9
  N10: R5.Pin_1, Part1.D6_PWM
  N11: R6.Pin_0, IC1.pin10
  N12: R6.Pin_1, Part1.D7
  N13: R7.Pin_0, IC1.pin13
  N14: R7.Pin_1, Part1.D9_PWM
  N15: R8.Pin_0, IC1.pin11
  N16: R8.Pin_1, Part1.D8

notes:
  This IC is a placeholder for a 7-segment display
  E
  +H+F+
  A G D
  +B+C+
  1: A
  2: B
  3: ?
  4: -
  5: -
  6: ?
  7: C
  8: D
  9: E
  10: F
  11: G
  12: -
  13: H
  14: GND
