# Fritzing sketch Sensor (saved by Fritzing 0.8.0b)
breadboards: 2

parts:
  Part1 = Arduino Uno (Rev3)
  Part2 = Arduino Uno (Rev3)
  S2 = Photocell (LDR) [package=THT]
  R4 = Resistor [tolerance=±5% resistance=1k package=THT]
  S3 = Photocell (LDR) [package=THT]
  R5 = Resistor [tolerance=±5% resistance=1k package=THT]  # not connected

nets:
  N1: Part1.A0, R4.Pin_1
  N2: Part1.5V, S2.pin_0
  N3: Part2.5V, S3.pin_0
  N4: S2.pin_1, R4.Pin_0

notes:
  1: Direct op input
