# Fritzing sketch AnalogRead (saved by Fritzing 0.8.0b)
breadboards: 5

parts:
  A1 = Arduino Uno (Rev3)
  A2 = Arduino Uno (Rev3)
  R4 = Resistor [tolerance=±5% resistance=1k package=THT]
  R5 = Resistor [tolerance=±5% resistance=1k package=THT]
  R6 = Resistor [tolerance=±5% resistance=1k package=THT]
  R7 = Resistor [tolerance=±5% resistance=1k package=THT]
  A3 = Arduino Uno (Rev3)
  R8 = Resistor [tolerance=±5% resistance=1k package=THT]
  R9 = Resistor [tolerance=±5% resistance=10k package=THT]
  A4 = Arduino Uno (Rev3)
  R10 = Resistor [tolerance=±5% resistance=10k package=THT]
  R11 = Resistor [tolerance=±5% resistance=1k package=THT]
  A5 = Arduino Uno (Rev3)
  R12 = Resistor [tolerance=±5% resistance=1k package=THT]
  R13 = Resistor [tolerance=±5% resistance=1k package=THT]

nets:
  N1: A1.A0, R4.Pin_1
  N2: A1.5V, R6.Pin_1
  N3: A2.A0, R5.Pin_0, R7.Pin_0
  N4: A2.GND, R5.Pin_1
  N5: A2.5V, R7.Pin_1
  N6: R4.Pin_0, R6.Pin_0
  N7: A3.A0, R8.Pin_0, R9.Pin_0
  N8: A3.GND, R8.Pin_1
  N9: A3.5V, R9.Pin_1
  N10: A4.A0, R10.Pin_0, R11.Pin_0
  N11: A4.GND, R10.Pin_1
  N12: A4.5V, R11.Pin_1
  N13: A5.A0, R13.Pin_1
  N14: A5.GND, R12.Pin_1
  N15: R12.Pin_0, R13.Pin_0

notes:
  1: Twee weerstanden van 1 kOhm achter elkaar, vanaf 5 Volt
  2: Tussen twee gelijke weerstanden van 1 kOhm in
  3: Tussen twee verschillende weerstanden in:
  10 kOhm, dan 1 kOhm
  4: Tussen twee verschillende weerstanden in:
  1 kOhm, dan 10 kOhm
  5: Twee weerstanden van 1 kOhm achter elkaar, vanaf Aarde
