# Fritzing sketch ArduinoCourseConnectPotMeter (saved by Fritzing 0.8.5b)
breadboards: 2

parts:
  R1 = Trimmer Potentiometer [maximum_resistance=10kΩ package=THT]
  R2 = Rotary Potentiometer (Small) [maximum_resistance=100kΩ package=THT]
  Part1 = Arduino Uno (Rev3)
  Part2 = Arduino Uno (Rev3)
  R3 = Resistor [tolerance=±5% resistance=1k package=THT]
  R4 = Resistor [tolerance=±5% resistance=1k package=THT]

nets:
  N1: R1.leg1, R2.leg1, Part1.5V
  N2: R1.leg2, R2.leg2, Part1.GND
  N3: R2.wiper, Part1.D3_PWM
  N4: Part2.GND, R4.Pin_1
  N5: Part2.D2, R3.Pin_1, R4.Pin_0
  N6: Part2.5V, R3.Pin_0
