# Fritzing sketch ArduinoCourseProjectColorSensor (saved by Fritzing 0.8.5b)
breadboards: 4

parts:
  R1 = Photocell (LDR) [package=THT]
  R2 = Photocell (LDR) [package=THT]
  R3 = Resistor [tolerance=±5% resistance=1k package=THT]
  LED1 = RGB LED (com. cathode, rgb) [package="5 mm [THT]"]
  LED2 = RGB LED (com. cathode, rgb) [package="5 mm [THT]"]
  R7 = Resistor [tolerance=±5% resistance=1k package=THT]
  R8 = Resistor [tolerance=±5% resistance=1k package=THT]
  R9 = Resistor [tolerance=±5% resistance=1k package=THT]
  Onderdeel2 = Arduino Uno (Rev3)
  Onderdeel1 = Arduino Uno (Rev3)
  Onderdeel3 = Arduino Uno (Rev3)
  Onderdeel4 = Arduino Uno (Rev3)

nets:
  N1: R1.pin_0, Onderdeel1.5V
  N2: R1.pin_1, Onderdeel1.A0
  N3: R2.pin_0, Onderdeel2.5V
  N4: R2.pin_1, R3.Pin_0, Onderdeel2.A0
  N5: R3.Pin_1, Onderdeel2.GND
  N6: LED1.red_anode, Onderdeel3.D11_PWM/MOSI
  N7: LED1.common_cathode, Onderdeel3.GND
  N8: LED1.green_anode, Onderdeel3.D10_PWM/SS
  N9: LED1.blue_anode, Onderdeel3.D9_PWM
  N10: LED2.red_anode, R7.Pin_0
  N11: LED2.common_cathode, Onderdeel4.GND
  N12: LED2.green_anode, R9.Pin_0
  N13: LED2.blue_anode, R8.Pin_0
  N14: R7.Pin_1, Onderdeel4.D11_PWM/MOSI
  N15: R8.Pin_1, Onderdeel4.D9_PWM
  N16: R9.Pin_1, Onderdeel4.D10_PWM/SS

notes:
  Naief: welke waarde zul je altijd meten op A0?
  De langste pin moet naar GND. De andere pinnen moeten naar een Arduino pin met een golfje
  ONJUIST!
  De langste pin moet naar GND. De andere pinnen moeten naar een Arduino pin met een golfje
