# Fritzing sketch Leds (saved by Fritzing 0.8.5b)
breadboards: 1

parts:
  Arduino1 = Arduino Uno (Rev3)
  LED1 = LED - 5mm [color="Red (633nm)" package="5 mm [THT]"]
  LED2 = LED - 5mm [color="Red (633nm)" package="5 mm [THT]"]
  R18 = Resistor [tolerance=±5% resistance=1k package=THT]
  R19 = Resistor [tolerance=±5% resistance=1k package=THT]
  LED3 = LED - 5mm [color="Red (633nm)" package="5 mm [THT]"]
  LED4 = LED - 5mm [color="Red (633nm)" package="5 mm [THT]"]
  R20 = Resistor [tolerance=±5% resistance=1k package=THT]
  R21 = Resistor [tolerance=±5% resistance=1k package=THT]
  LED5 = LED - 5mm [color="Red (633nm)" package="5 mm [THT]"]
  LED6 = LED - 5mm [color="Red (633nm)" package="5 mm [THT]"]
  LED7 = LED - 5mm [color="Red (633nm)" package="5 mm [THT]"]
  LED8 = LED - 5mm [color="Red (633nm)" package="5 mm [THT]"]
  R22 = Resistor [tolerance=±5% resistance=1k package=THT]
  R23 = Resistor [tolerance=±5% resistance=1k package=THT]
  R24 = Resistor [tolerance=±5% resistance=1k package=THT]
  R25 = Resistor [tolerance=±5% resistance=1k package=THT]
  LED9 = LED - 5mm [color="Red (633nm)" package="5 mm [THT]"]
  LED10 = LED - 5mm [color="Red (633nm)" package="5 mm [THT]"]
  R26 = Resistor [tolerance=±5% resistance=1k package=THT]
  R27 = Resistor [tolerance=±5% resistance=1k package=THT]
  LED11 = LED - 5mm [color="Red (633nm)" package="5 mm [THT]"]
  LED12 = LED - 5mm [color="Red (633nm)" package="5 mm [THT]"]
  R28 = Resistor [tolerance=±5% resistance=1k package=THT]
  R29 = Resistor [tolerance=±5% resistance=1k package=THT]

nets:
  N1: Arduino1.GND, R18.Pin_1, R19.Pin_1, R20.Pin_1, R21.Pin_1, R22.Pin_1, R23.Pin_1, R24.Pin_1, R25.Pin_1, R26.Pin_1, R27.Pin_1, R28.Pin_1, R29.Pin_1
  N2: Arduino1.D8, LED8.anode
  N3: Arduino1.D9_PWM, LED7.anode
  N4: Arduino1.D10_PWM/SS, LED9.anode
  N5: Arduino1.D11_PWM/MOSI, LED10.anode
  N6: Arduino1.D12/MISO, LED11.anode
  N7: Arduino1.D13/SCK, LED12.anode
  N8: Arduino1.D2, LED1.anode
  N9: Arduino1.D3_PWM, LED2.anode
  N10: Arduino1.D4, LED3.anode
  N11: Arduino1.D5_PWM, LED4.anode
  N12: Arduino1.D6_PWM, LED5.anode
  N13: Arduino1.D7, LED6.anode
  N14: LED1.cathode, R18.Pin_0
  N15: LED2.cathode, R19.Pin_0
  N16: LED3.cathode, R20.Pin_0
  N17: LED4.cathode, R21.Pin_0
  N18: LED5.cathode, R22.Pin_0
  N19: LED6.cathode, R23.Pin_0
  N20: LED7.cathode, R24.Pin_0
  N21: LED8.cathode, R25.Pin_0
  N22: LED9.cathode, R26.Pin_0
  N23: LED10.cathode, R27.Pin_0
  N24: LED11.cathode, R28.Pin_0
  N25: LED12.cathode, R29.Pin_0
