# Fritzing sketch SchematicThatCannotWork (saved by Fritzing 0.8.0b)
breadboards: 1

parts:
  V1 = DC Power [voltage=5]
  LED1 = LED - 5mm [color="Red (633nm)" package="5 mm [THT]"]
  LED2 = LED - 5mm [color="Red (633nm)" package="5 mm [THT]"]

nets:
  N1: V1.V+, LED1.anode
  N2: V1.V-, LED1.cathode, LED2.cathode, LED2.anode
