# Fritzing sketch 2_knop_if_else (saved by Fritzing 0.9.0b)
breadboards: 1

parts:
  LED1 = LED - 5mm [color="Red (633nm)" package="5 mm [THT]"]
  Part1 = Arduino Uno (Rev3)
  R1 = Resistor [tolerance=±5% resistance=1k package=THT]  # not connected
  S1 = Pushbutton [package="[THT]"]
  R2 = Resistor [tolerance=±5% resistance=10k package=THT]

nets:
  N1: LED1.anode, Part1.D13/SCK
  N2: Part1.GND, R2.Pin_0
  N3: Part1.D2, S1.Pin_1, S1.Pin_2, R2.Pin_1
  N4: Part1.5V, S1.Pin_3, S1.Pin_4
