# Fritzing sketch BlinkBlinkBlink (saved by Fritzing 0.8.5b)
breadboards: 1

parts:
  R1 = Resistor [tolerance=±5% resistance=1k package=THT]
  LED1 = LED - 5mm [color="Red (633nm)" package="5 mm [THT]"]
  R2 = Resistor [tolerance=±5% resistance=1k package=THT]
  LED2 = LED - 5mm [color="Green (555nm)" package="5 mm [THT]"]
  R3 = Resistor [tolerance=±5% resistance=1k package=THT]
  LED3 = LED - 5mm [color="Blue (430nm)" package="5 mm [THT]"]
  Part1 = Arduino Uno (Rev3)

nets:
  N1: R1.Pin_0, LED1.cathode
  N2: LED1.anode, Part1.D11_PWM/MOSI
  N3: R2.Pin_0, LED2.cathode
  N4: R2.Pin_1, R3.Pin_1, Part1.GND
  N5: LED2.anode, Part1.D10_PWM/SS
  N6: R3.Pin_0, LED3.cathode
  N7: LED3.anode, Part1.D9_PWM
